// Digital circuit PDP8-X.dig as structural Verilog
module PDP8_X (
  input  clk
);

  wire AC2RAMD, AC_CK, add_1_c_o, add_2_c_o, AND, and_1_out, and_3_out, and_4_out, and_6_out, and_8_out,
       and_9_out, and_11_out, and_12_out, and_13_out, and_14_out, and_15_out, and_17_out, and_18_out,
       and_19_out, and_21_out, and_22_out, and_23_out, and_24_out, and_26_out, and_27_out, and_28_out,
       and_29_out, and_31_out, and_33_out, and_34_out, and_35_out, and_37_out, and_38_out, and_39_out,
       and_40_out, and_41_out, and_42_out, and_43_out, and_45_out, and_46_out, and_47_out, and_48_out,
       and_50_out, and_51_out, and_52_out, and_53_out, and_54_out, and_55_out, and_56_out, and_57_out,
       and_58_out, and_59_out, and_60_out, and_61_out, and_62_out, and_64_out, and_65_out, and_66_out,
       and_68_out, and_69_out, and_71_out, and_72_out, and_73_out, and_74_out, and_76_out, and_77_out,
       and_78_out, and_79_out, and_80_out, and_81_out, and_82_out, and_83_out, and_85_out, and_86_out,
       and_87_out, and_88_out, and_90_out, and_91_out, and_92_out, and_93_out, and_94_out, and_95_out,
       and_96_out, and_97_out, and_98_out, and_99_out, and_100_out, and_101_out, and_102_out, and_104_out,
       and_105_out, and_106_out, and_108_out, and_110_out, and_111_out, and_112_out, and_114_out,
       and_115_out, and_116_out, and_118_out, and_120_out, and_121_out, and_122_out, and_124_out,
       and_125_out, and_126_out, and_127_out, and_128_out, and_129_out, and_150_out, and_154_out,
       and_156_out, AUTOIND, BP_ENABLED_b, CK0, CK1, CK2, CK3, CK4, CK5, CK6, CK7, CK8, CK9, CLA, CLAx,
       CNT_AND, CNT_AND_I, CNT_AND_IA, CNT_DCA, CNT_DCA_I, CNT_DCA_IA, CNT_ISZ, CNT_ISZ_I, CNT_ISZ_IA,
       CNT_JMP, CNT_JMP_I, CNT_JMP_IA, CNT_JMS, CNT_JMS_I, CNT_JMS_IA, CNT_OPR1, CNT_OPR2, CNT_OPR3, CNT_TAD,
       CNT_TAD_I, CNT_TAD_IA, comparator_1_eq, comparator_2_eq, counter_1_o1, counter_1_o2, counter_1_o3,
       counter_1_o4, counter_1_o5, counter_1_o6, counter_1_o7, counter_1_o8, counter_1_o9, counter_1_o10,
       counter_1_o11, counter_1_o12, counter_1_o13, counter_1_o14, counter_1_o15, counter_1_o16,
       counter_1_o17, counter_1_o18, counter_1_o19, counter_1_o20, counter_1_o21, counter_1_o22,
       counter_1_o23, counter_1_o24, counter_1_o25, counter_1_o26, counter_1_o27, counter_1_o28,
       counter_1_o29, counter_1_o30, counter_1_o31, counter_1_o32, counter_2_ovf, d_ff_1_q, DATA_CK, DCA,
       demultiplexer_1_out_3, demultiplexer_1_out_7, demultiplexer_2_out_3, demultiplexer_2_out_7,
       demultiplexer_3_out_0, demultiplexer_3_out_1, demultiplexer_3_out_2, demultiplexer_3_out_3,
       demultiplexer_3_out_4, demultiplexer_3_out_5, demultiplexer_3_out_6, demultiplexer_3_out_7,
       demultiplexer_5_out_10, demultiplexer_5_out_11, demultiplexer_5_out_12, demultiplexer_5_out_13,
       demultiplexer_5_out_14, demultiplexer_5_out_15, demultiplexer_5_out_16, demultiplexer_5_out_17,
       demultiplexer_5_out_18, demultiplexer_5_out_19, demultiplexer_5_out_20, demultiplexer_5_out_21,
       demultiplexer_5_out_22, demultiplexer_5_out_23, demultiplexer_5_out_24, demultiplexer_5_out_25,
       demultiplexer_5_out_26, demultiplexer_5_out_27, demultiplexer_5_out_28, demultiplexer_5_out_29,
       demultiplexer_5_out_30, demultiplexer_5_out_31, demultiplexer_5_out_32, demultiplexer_5_out_33,
       demultiplexer_5_out_34, demultiplexer_5_out_35, demultiplexer_5_out_36, demultiplexer_5_out_37,
       demultiplexer_5_out_38, demultiplexer_5_out_39, demultiplexer_5_out_40, demultiplexer_5_out_41,
       demultiplexer_5_out_42, demultiplexer_5_out_43, demultiplexer_5_out_44, demultiplexer_5_out_45,
       demultiplexer_5_out_46, demultiplexer_5_out_47, demultiplexer_5_out_48, demultiplexer_5_out_49,
       demultiplexer_5_out_50, demultiplexer_5_out_51, demultiplexer_5_out_52, demultiplexer_5_out_53,
       demultiplexer_5_out_54, demultiplexer_5_out_55, demultiplexer_5_out_56, demultiplexer_5_out_57,
       demultiplexer_5_out_58, demultiplexer_5_out_59, demultiplexer_5_out_60, demultiplexer_5_out_61,
       demultiplexer_5_out_62, demultiplexer_5_out_63, demultiplexer_7_out_0, demultiplexer_7_out_1,
       driver_1_out, driver_84_out, driver_85_out, driver_260_out, driver_261_out, driver_266_out,
       driver_285_out, driver_286_out, driver_291_out, driver_319_out, driver_322_out, driver_323_out,
       driver_324_out, driver_328_out, driver_329_out, driver_330_out, driver_331_out, driver_332_out,
       driver_333_out, driver_334_out, driver_336_out, driver_337_out, driver_338_out, driver_343_out,
       driver_344_out, driver_349_out, driver_353_out, driver_354_out, driver_364_out, driver_367_out,
       driver_368_out, driver_369_out, driver_371_out, driver_372_out, driver_373_out, driver_386_out,
       driver_387_out, driver_392_out, driver_396_out, driver_397_out, driver_407_out, driver_410_out,
       driver_411_out, driver_412_out, driver_414_out, driver_415_out, driver_416_out, driver_425_out,
       driver_435_out, driver_457_out, FLAG_PRNRDY, H_out, HALT, HLT_ENABLED_b, i_cla, i_cll, i_cma, i_cml,
       i_hlt, i_iac, i_nop, i_osr, I_out, i_ral, i_rar, i_rtl, i_rtr, i_skp, i_sma, i_sna, i_snl, i_spa,
       i_sza, i_szl, INC2RAMD, INCZERO, IND, IND2INC, IND2PC, IND2RAMA, IND_CK, INST_KCC, INST_KCF, INST_KIE,
       INST_KRB, INST_KRS, INST_KSF, INST_TCF, INST_TFL, INST_TLS, INST_TPC, INST_TSF, INST_TSK, IOT, IOT_1x,
       IOT_2x, IOT_3x, IOT_4x, IOT_5, IOT_5x, IOT_6, IOT_6x, IOT_7, IOT_8, IOT_9, IOT_CAF, IOT_DEVCPU,
       IOT_DEVHSP, IOT_DEVHSR, IOT_DEVKBD, IOT_DEVPRI, IOT_GTF, IOT_IOF, IOT_ION, IOT_RTF, IOT_SGT, IOT_SKON,
       IOT_SRQ, IR2PC, IR2RAMA, IR_CK, ISZ, JMP, JMS, LD2INC, LINK, LINK_CK, monoflop_1_q, monoflop_2_q,
       monoflop_3_nq, monoflop_3_q, monoflop_4_q, monoflop_5_q, MP, MQ_CK, nand_1_out, NOIND, nor_1_out,
       nor_2_out, nor_3_out, nor_4_out, not_1_out, not_2_out, not_4_out, not_5_out, not_6_out, OPR, OPR1,
       OPR2, OPR3, OPR_ASL, OPR_CLA1, OPR_CLA2, OPR_CLA3, OPR_CLL, OPR_CMA, OPR_CML, OPR_DVI, OPR_HLT,
       OPR_IAC, OPR_LEFT, OPR_LSR, OPR_MQA, OPR_MQL, OPR_MUY, OPR_NA1, OPR_NMI, OPR_NOP, OPR_OPERATION,
       OPR_OSR, OPR_RIGHT, OPR_SCA, OPR_SCL, OPR_SHL, OPR_SMASPA, OPR_SNLSZL, OPR_SWP, OPR_SZASNA,
       OPR_TSTINV, OPR_X2, or_1_out, or_2_out, or_3_out, or_5_out, or_6_out, or_7_out, or_8_out, or_9_out,
       or_10_out, PC2ADDR, PC2RAMD, PC_CK, PC_eq_200, PC_LD, PH_FIRST, PH_LAST, PH_STB, R_out, RAM_OE,
       RAM_WE, RAMA_HOLD, RAMD2AC_ADD, RAMD2AC_AND, RAMD2IND, RAMD2PC, reset_1_out, ROT2AC, rotater_1_p5,
       rs_ff_as_1_q, rs_ff_as_2_q, S_out, SKIP, STB0, STB1, STB2, STB3, STB4, STB5, STB6, STB7, STB8, STB9,
       TAD, TAD_OVF_q, xor_1_out, xor_2_out, xor_3_out, xor_4_out, xor_5_out;
  wire [2:0] and_151_out, DA0, DA1, DA2, DA3, IND0, IND1, IND2, IND3, RA0, RA1, RA2, RA3;
  wire [3:0] CK_NUM;
  wire [4:0] counter_2_out;
  wire [11:0] AC, add_1_s, add_2_s, and_2_out, and_5_out, and_7_out, autocapture_1__10, autocapture_1__11,
       autocapture_1__12, autocapture_1__13, autocapture_1__14, autocapture_1__15, autocapture_1__16,
       autocapture_1__17, bitextender_1_out, bitextender_2_out, bitextender_3_out, BUS_IR, BUS_PC,
       dipswitch_1_out, driver_6_out, driver_14_out, driver_18_out, INC_s, LATCHED_PC, LATCHEDDATA, MQ,
       not_3_out, or_4_out, PCIN, RAMDATA, register_1_q, rotater_1_p4, xor_6_out;
  wire [31:0] COUNT_out, INSTRUCTION_COUNT_out;

  Comparator #(.Bits(12)) comparator_1 (.a({RA3, RA2, RA1, RA0}), .b(12'h5a7), .eq(comparator_1_eq));  // open: gt, lt
  xor xor_1 (xor_1_out, CK0, PC_eq_200);
  and and_1 (and_1_out, comparator_1_eq, RAM_WE);
  assign driver_1_out = PC_eq_200 ? PC_eq_200 : 1'bz;  // Driver driver_1
  assign PC_LD = PC_eq_200 ? PC_eq_200 : 1'bz;  // Driver driver_2
  LED led_1 (.in(IR2PC));
  assign PCIN = PC_eq_200 ? 12'h80 : 12'bz;  // Driver driver_3
  COUNTER counter_1 (
    .i1(CNT_AND), .i2(CNT_AND_I), .i3(CNT_AND_IA), .i4(CNT_TAD), .i5(CNT_TAD_I), .i6(CNT_TAD_IA),
    .i7(CNT_ISZ), .i8(CNT_ISZ_I), .i9(CNT_ISZ_IA), .i10(CNT_DCA), .i11(CNT_DCA_I), .i12(CNT_DCA_IA),
    .i13(CNT_JMS), .i14(CNT_JMS_I), .i15(CNT_JMS_IA), .i16(CNT_JMP), .i17(CNT_JMP_I), .i18(CNT_JMP_IA),
    .i19(CNT_OPR1), .i20(CNT_OPR2), .i21(IOT_DEVCPU), .i22(IOT_DEVHSR), .i23(IOT_DEVHSP), .i24(IOT_DEVKBD),
    .i25(IOT_DEVPRI), .i26(IOT_5), .i27(IOT_6), .i28(IOT_7), .i29(IOT_8), .i30(IOT_9), .i31(IOT_1x),
    .i32(IOT_2x), .C(1'b0), .E(1'b1), .o1(counter_1_o1), .o2(counter_1_o2), .o3(counter_1_o3),
    .o4(counter_1_o4), .o5(counter_1_o5), .o6(counter_1_o6), .o7(counter_1_o7), .o8(counter_1_o8),
    .o9(counter_1_o9), .o10(counter_1_o10), .o11(counter_1_o11), .o12(counter_1_o12), .o13(counter_1_o13),
    .o14(counter_1_o14), .o15(counter_1_o15), .o16(counter_1_o16), .o17(counter_1_o17), .o18(counter_1_o18),
    .o19(counter_1_o19), .o20(counter_1_o20), .o21(counter_1_o21), .o22(counter_1_o22), .o23(counter_1_o23),
    .o24(counter_1_o24), .o25(counter_1_o25), .o26(counter_1_o26), .o27(counter_1_o27), .o28(counter_1_o28),
    .o29(counter_1_o29), .o30(counter_1_o30), .o31(counter_1_o31), .o32(counter_1_o32));
  AUTOCAPTURE autocapture_1 (
    .D(RAMDATA), .A({RA3, RA2, RA1, RA0}), .WR(RAM_WE), ._10(autocapture_1__10), ._11(autocapture_1__11),
    ._12(autocapture_1__12), ._13(autocapture_1__13), ._14(autocapture_1__14), ._15(autocapture_1__15),
    ._16(autocapture_1__16), ._17(autocapture_1__17));
  Counter #(.Bits(32)) INSTRUCTION_COUNT (.en(1'b1), .C(CK0), .clr(1'b0), .out(INSTRUCTION_COUNT_out));  // open: ovf
  Register #(.Bits(12)) register_1 (.D(RAMDATA), .C(and_1_out), .en(1'b1), .Q(register_1_q));
  Register #(.Bits(12)) register_2 (.D(BUS_PC), .C(xor_1_out), .en(1'b1), .Q(LATCHED_PC));
  // OC12 oc12_1: pin names not known; wires that end beside it: BUS_IR[6:0], BUS_PC[11:7], MP, IR2PC, PCIN[6:0], PCIN[11:7], PCIN
  // Probe on counter_1_o1
  // Probe on counter_1_o2
  // Probe on counter_1_o3
  // Probe on counter_1_o4
  // Probe on counter_1_o5
  // Probe on counter_1_o6
  // Probe on counter_1_o7
  // Probe on counter_1_o8
  // Probe on counter_1_o9
  // Probe on counter_1_o10
  // Probe on counter_1_o11
  // Probe on counter_1_o12
  // Probe on counter_1_o13
  // Probe on counter_1_o14
  // Probe on counter_1_o15
  // Probe on counter_1_o16
  // Probe on counter_1_o17
  // Probe on counter_1_o18
  // Probe on counter_1_o19
  // Probe on counter_1_o20
  // Probe on counter_1_o21
  // Probe on counter_1_o22
  // Probe on counter_1_o23
  // Probe on counter_1_o24
  // Probe on counter_1_o25
  // Probe on counter_1_o26
  // Probe on counter_1_o27
  // Probe on counter_1_o28
  // Probe on counter_1_o29
  // Probe on counter_1_o30
  // Probe on counter_1_o31
  // Probe on counter_1_o32
  // Probe on autocapture_1__10
  // Probe on autocapture_1__11
  // Probe on autocapture_1__12
  // Probe on autocapture_1__13
  // Probe on autocapture_1__14
  // Probe on autocapture_1__15
  // Probe on autocapture_1__16
  // Probe on autocapture_1__17
  // Probe on INSTRUCTION_COUNT_out
  // Probe on register_1_q
  // Probe on PCIN
  LED led_2 (.in(PC_CK));
  LED led_3 (.in(RAMD2PC));
  assign PCIN = RAMD2PC ? {DA3, DA2, DA1, DA0} : 12'bz;  // Driver driver_4
  LED led_4 (.in(IND2PC));
  assign PCIN = IND2PC ? {IND3, IND2, IND1, IND0} : 12'bz;  // Driver driver_5
  LED led_5 (.in(LINK));
  // Probe on {DA3, DA2, DA1, DA0}
  ROM #(.AddrBits(5), .Bits(8)) APA (.A(5'b00001), .sel(1'b1));  // open: D
  xor xor_2 (xor_2_out, PC_CK, driver_1_out);
  Seven_Seg_Hex seven_seg_hex_1 (.d({1'b0, BUS_PC[11:9]}), .dp(1'b0));
  Seven_Seg_Hex seven_seg_hex_2 (.d({1'b0, BUS_IR[11:9]}), .dp(1'b0));
  Seven_Seg_Hex seven_seg_hex_3 (.d({1'b0, AC[11:9]}), .dp(1'b0));
  Seven_Seg_Hex seven_seg_hex_4 (.d({1'b0, MQ[11:9]}), .dp(1'b0));
  Seven_Seg_Hex seven_seg_hex_5 (.d({1'b0, IND3}), .dp(1'b0));
  Seven_Seg_Hex seven_seg_hex_6 (.d({1'b0, RA3}), .dp(1'b0));
  Seven_Seg_Hex seven_seg_hex_7 (.d({1'b0, RAMDATA[11:9]}), .dp(1'b0));
  Seven_Seg_Hex seven_seg_hex_8 (.d({1'b0, PCIN[11:9]}), .dp(1'b0));
  Seven_Seg_Hex seven_seg_hex_9 (.d({1'b0, DA3}), .dp(1'b0));
  not not_1 (not_1_out, xor_2_out);
  LED led_6 (.in(PC_LD));
  Seven_Seg_Hex seven_seg_hex_10 (.d({1'b0, BUS_PC[8:6]}), .dp(1'b0));
  Seven_Seg_Hex seven_seg_hex_11 (.d({1'b0, BUS_IR[8:6]}), .dp(1'b0));
  Seven_Seg_Hex seven_seg_hex_12 (.d({1'b0, AC[8:6]}), .dp(1'b0));
  Seven_Seg_Hex seven_seg_hex_13 (.d({1'b0, MQ[8:6]}), .dp(1'b0));
  Seven_Seg_Hex seven_seg_hex_14 (.d({1'b0, IND2}), .dp(1'b0));
  Seven_Seg_Hex seven_seg_hex_15 (.d({1'b0, RA2}), .dp(1'b0));
  Seven_Seg_Hex seven_seg_hex_16 (.d({1'b0, RAMDATA[8:6]}), .dp(1'b0));
  Seven_Seg_Hex seven_seg_hex_17 (.d({1'b0, PCIN[8:6]}), .dp(1'b0));
  Seven_Seg_Hex seven_seg_hex_18 (.d({1'b0, DA2}), .dp(1'b0));
  LED led_7 (.in(RAMD2AC_ADD));
  ROM #(.AddrBits(5), .Bits(8)) BANAN (.A(5'b00001), .sel(1'b1));  // open: D
  CounterPreset #(.Bits(12)) PC (
    .en(1'b1), .C(not_1_out), .dir(1'b0), .in(PCIN), .ld(PC_LD), .clr(reset_1_out), .out(BUS_PC));  // open: ovf
  Seven_Seg_Hex seven_seg_hex_19 (.d({1'b0, BUS_PC[5:3]}), .dp(1'b0));
  Seven_Seg_Hex seven_seg_hex_20 (.d({1'b0, BUS_IR[5:3]}), .dp(1'b0));
  Seven_Seg_Hex seven_seg_hex_21 (.d({1'b0, AC[5:3]}), .dp(1'b0));
  Seven_Seg_Hex seven_seg_hex_22 (.d({1'b0, MQ[5:3]}), .dp(1'b0));
  Seven_Seg_Hex seven_seg_hex_23 (.d({1'b0, IND1}), .dp(1'b0));
  Seven_Seg_Hex seven_seg_hex_24 (.d({1'b0, RA1}), .dp(1'b0));
  Seven_Seg_Hex seven_seg_hex_25 (.d({1'b0, RAMDATA[5:3]}), .dp(1'b0));
  Seven_Seg_Hex seven_seg_hex_26 (.d({1'b0, PCIN[5:3]}), .dp(1'b0));
  Seven_Seg_Hex seven_seg_hex_27 (.d({1'b0, DA1}), .dp(1'b0));
  assign and_2_out = AC & {DA3, DA2, DA1, DA0};  // And and_2, 12 bits wide
  Add #(.Bits(12)) add_1 (.a(AC), .b({DA3, DA2, DA1, DA0}), .c_i(1'b0), .s(add_1_s), .c_o(add_1_c_o));
  and and_3 (and_3_out, add_1_c_o, RAMD2AC_ADD);
  LED led_8 (.in(and_3_out));
  Reset #(.invertOutput("false")) reset_1 (.out(reset_1_out));
  Seven_Seg_Hex seven_seg_hex_28 (.d({1'b0, BUS_PC[2:0]}), .dp(1'b0));
  Seven_Seg_Hex seven_seg_hex_29 (.d({1'b0, BUS_IR[2:0]}), .dp(1'b0));
  Seven_Seg_Hex seven_seg_hex_30 (.d({1'b0, AC[2:0]}), .dp(1'b0));
  Seven_Seg_Hex seven_seg_hex_31 (.d({1'b0, MQ[2:0]}), .dp(1'b0));
  Seven_Seg_Hex seven_seg_hex_32 (.d({1'b0, IND0}), .dp(1'b0));
  Seven_Seg_Hex seven_seg_hex_33 (.d({1'b0, RA0}), .dp(1'b0));
  Seven_Seg_Hex seven_seg_hex_34 (.d({1'b0, RAMDATA[2:0]}), .dp(1'b0));
  Seven_Seg_Hex seven_seg_hex_35 (.d({1'b0, PCIN[2:0]}), .dp(1'b0));
  Seven_Seg_Hex seven_seg_hex_36 (.d({1'b0, DA0}), .dp(1'b0));
  // Probe on AC
  // Probe on and_2_out
  // Probe on add_1_s
  LED led_9 (.in(add_1_c_o));
  // Probe on rotater_1_p4
  D_FF TAD_OVF (.D(and_3_out), .C(STB1), .Q(TAD_OVF_q));  // open: nQ
  LED led_10 (.in(STB1));
  // Probe on BUS_PC
  and and_4 (and_4_out, OPR_MQL, MQ_CK);
  LED led_11 (.in(MQ_CK));
  LED led_12 (.in(TAD_OVF_q));
  // OC12 oc12_2: pin names not known; wires that end beside it: BUS_PC, BUS_IR[6:0], BUS_PC[11:7], MP, IR2RAMA, {RA2[0], RA1, RA0}, {RA3, RA2[2:1]}
  LED led_13 (.in(IR2RAMA));
  LED led_14 (.in(INST_KCF));
  LED led_15 (.in(i_nop));
  LED led_16 (.in(AND));
  LED led_17 (.in(and_4_out));
  assign driver_6_out = RAMD2AC_AND ? and_2_out : 12'bz;  // Driver driver_6
  LED led_18 (.in(RAMD2AC_AND));
  assign driver_6_out = RAMD2AC_ADD ? add_1_s : 12'bz;  // Driver driver_7
  LED led_19 (.in(RAMD2AC_ADD));
  assign driver_6_out = ROT2AC ? rotater_1_p4 : 12'bz;  // Driver driver_8
  LED led_20 (.in(ROT2AC));
  xor xor_3 (xor_3_out, TAD_OVF_q, rotater_1_p5);
  LED led_21 (.in(PC2ADDR));
  assign {RA3, RA2, RA1, RA0} = PC2ADDR ? BUS_PC : 12'bz;  // Driver driver_9
  LED led_22 (.in(INST_KSF));
  LED led_23 (.in(i_cla));
  LED led_24 (.in(TAD));
  // Probe on and_5_out
  // Probe on driver_6_out
  LED led_25 (.in(xor_3_out));
  // Probe on {RA3, RA2, RA1, RA0}
  LED led_26 (.in(IND2RAMA));
  LED led_27 (.in(INST_KCC));
  LED led_28 (.in(INST_KRS));
  LED led_29 (.in(i_cll));
  LED led_30 (.in(ISZ));
  LED led_31 (.in(DCA));
  Button S (.out(S_out));
  Button I (.out(I_out));
  Button R (.out(R_out));
  Button H (.out(H_out));
  Button P (.out(PC_eq_200));
  assign and_5_out = AC & ~bitextender_1_out;  // And and_5, 12 bits wide
  LED led_32 (.in(AC_CK));
  D_FF u_LINK (.D(xor_3_out), .C(LINK_CK), .Q(LINK));  // open: nQ
  LED led_33 (.in(LINK_CK));
  LED led_34 (.in(RAM_WE));
  LED led_35 (.in(RAM_OE));
  assign {RA3, RA2, RA1, RA0} = IND2RAMA ? {IND3, IND2, IND1, IND0} : 12'bz;  // Driver driver_10
  LED led_36 (.in(INST_KIE));
  LED led_37 (.in(i_cma));
  LED led_38 (.in(JMS));
  Monoflop #(.timerDelay(2)) monoflop_1 (.C(I_out), .R(1'b0), .Q(monoflop_1_q));  // open: nQ
  Monoflop monoflop_2 (.C(R_out), .R(1'b0), .Q(monoflop_2_q));  // open: nQ
  D_FF #(.Bits(12)) u_MQ (.D(and_5_out), .C(and_4_out), .Q(MQ));  // open: nQ
  D_FF #(.Bits(12)) u_AC (.D(driver_6_out), .C(AC_CK), .Q(AC));  // open: nQ
  or or_1 (or_1_out, OPR_CLA1, OPR_CLA2, OPR_CLA3, OPR_MQL);
  LED led_39 (.in(LINK));
  EEPROM #(.AddrBits(15), .isProgramMemory("true"), .Bits(12)) eeprom_1 (
    .A({3'b001, RA3, RA2, RA1, RA0}), .CS(1'b1), .WE(RAM_WE), .OE(RAM_OE), .D(RAMDATA));
  LED led_40 (.in(INST_KRB));
  LED led_41 (.in(i_cml));
  LED led_42 (.in(JMP));
  Comparator #(.Bits(12)) comparator_2 (.a(BUS_PC), .b(12'h884), .eq(comparator_2_eq));  // open: gt, lt
  // Probe on MQ
  BitExtender #(.inputBits(1), .outputBits(12)) bitextender_1 (.in(OPR_CLA3), .out(bitextender_1_out));
  // Probe on AC
  BitExtender #(.inputBits(1), .outputBits(12)) bitextender_2 (.in(or_1_out), .out(bitextender_2_out));
  LED led_43 (.in(or_1_out));
  and and_6 (and_6_out, LINK, ~OPR_CLL);  // And
  LED led_44 (.in(OPR_CLL));
  // Probe on RAMDATA
  LED led_45 (.in(INST_TFL));
  LED led_46 (.in(i_iac));
  LED led_47 (.in(IOT));
  LED led_48 (.in(OPR));
  Switch #(.Closed("true")) HLT_ENABLED (.A(HALT), .B(HLT_ENABLED_b));
  assign and_7_out = AC & ~bitextender_2_out;  // And and_7, 12 bits wide
  LED led_49 (.in(and_6_out));
  assign {DA3, DA2, DA1, DA0} = RAM_OE ? RAMDATA : 12'bz;  // Driver driver_11
  assign RAMDATA = RAM_WE ? {DA3, DA2, DA1, DA0} : 12'bz;  // Driver driver_12
  LED led_50 (.in(INST_TSF));
  LED led_51 (.in(i_rar));
  LED led_52 (.in(i_rtr));
  RS_FF_AS rs_ff_as_1 (.S(monoflop_2_q), .R(or_3_out), .Q(rs_ff_as_1_q));  // open: nQ
  PullDown pulldown_1 (.out(HLT_ENABLED_b));
  Switch #(.Closed("true")) BP_ENABLED (.A(comparator_2_eq), .B(BP_ENABLED_b));
  // Probe on and_7_out
  LED led_53 (.in(OPR_CML));
  LED led_54 (.in(PC2RAMD));
  assign {DA3, DA2, DA1, DA0} = PC2RAMD ? BUS_PC : 12'bz;  // Driver driver_13
  LED led_55 (.in(INST_TCF));
  LED led_56 (.in(i_ral));
  LED led_57 (.in(NOIND));
  LED led_58 (.in(IND));
  or or_2 (or_2_out, monoflop_1_q, monoflop_2_q, rs_ff_as_1_q);
  or or_3 (or_3_out, H_out, BP_ENABLED_b, HLT_ENABLED_b);
  PullDown pulldown_2 (.out(BP_ENABLED_b));
  assign driver_14_out = OPR_MQA ? MQ : 12'bz;  // Driver driver_14
  LED led_59 (.in(OPR_MQA));
  xor xor_4 (xor_4_out, and_6_out, OPR_CML);
  // Probe on {DA3, DA2, DA1, DA0}
  LED led_60 (.in(INC2RAMD));
  assign {DA3, DA2, DA1, DA0} = INC2RAMD ? INC_s : 12'bz;  // Driver driver_15
  LED led_61 (.in(AC2RAMD));
  assign {DA3, DA2, DA1, DA0} = AC2RAMD ? AC : 12'bz;  // Driver driver_16
  LED led_62 (.in(INST_TPC));
  LED led_63 (.in(INST_TSK));
  LED led_64 (.in(i_rtl));
  LED led_65 (.in(AUTOIND));
  LED led_66 (.in(or_2_out));
  LED led_67 (.in(or_3_out));
  assign driver_14_out = OPR_OSR ? not_3_out : 12'bz;  // Driver driver_17
  LED led_68 (.in(OPR_OSR));
  // Probe on driver_14_out
  assign or_4_out = driver_14_out | and_7_out;  // Or or_4, 12 bits wide
  BitExtender #(.inputBits(1), .outputBits(12)) bitextender_3 (.in(OPR_CMA), .out(bitextender_3_out));
  LED led_69 (.in(OPR_CMA));
  LED led_70 (.in(xor_4_out));
  not not_2 (not_2_out, IR_CK);
  LED led_71 (.in(IR_CK));
  LED led_72 (.in(INST_TLS));
  LED led_73 (.in(i_skp));
  LED led_74 (.in(MP));
  D_FF d_ff_1 (.D(counter_2_ovf), .C(clk), .Q(d_ff_1_q));  // open: nQ
  // Probe on or_4_out
  xor xor_5 (xor_5_out, and_9_out, xor_4_out);
  // TRANSP_LATCH IR: pin names not known; wires that end beside it: {DA3, DA2, DA1, DA0}, {DA3, DA2, DA1, DA0}, not_2_out, BUS_IR, BUS_IR
  LED led_75 (.in(i_sza));
  LED led_76 (.in(i_sma));
  RS_FF_AS rs_ff_as_2 (.S(or_2_out), .R(d_ff_1_q), .Q(rs_ff_as_2_q));  // open: nQ
  // Probe on not_3_out
  assign xor_6_out = or_4_out ^ bitextender_3_out;  // XOr xor_6, 12 bits wide
  LED led_77 (.in(xor_5_out));
  // Probe on BUS_IR
  LED led_78 (.in(i_spa));
  and and_8 (and_8_out, rs_ff_as_2_q, clk);
  // Probe on xor_6_out
  LED led_79 (.in(OPR_IAC));
  D_FF #(.Bits(12)) u_IND (.D({DA3, DA2, DA1, DA0}), .C(IND_CK), .Q({IND3, IND2, IND1, IND0}));  // open: nQ
  LED led_80 (.in(IND_CK));
  LED led_81 (.in(i_sna));
  assign not_3_out = ~dipswitch_1_out;  // Not not_3, 12 bits wide
  Add #(.Bits(12)) add_2 (.a(xor_6_out), .b({12{1'b0}}), .c_i(OPR_IAC), .s(add_2_s), .c_o(add_2_c_o));
  LED led_82 (.in(i_szl));
  LED led_83 (.in(i_snl));
  or or_5 (or_5_out, S_out, and_8_out);
  LED led_84 (.in(or_5_out));
  DipSwitch dipswitch_1 (.out(dipswitch_1_out[11]));
  DipSwitch dipswitch_2 (.out(dipswitch_1_out[10]));
  DipSwitch dipswitch_3 (.out(dipswitch_1_out[9]));
  // Probe on add_2_s
  and and_9 (and_9_out, add_2_c_o, OPR_IAC);
  LED led_85 (.in(add_2_c_o));
  // Probe on {IND3, IND2, IND1, IND0}
  LED led_86 (.in(DATA_CK));
  LED led_87 (.in(i_osr));
  Counter #(.Bits(5)) counter_2 (
    .en(1'b1), .C(or_5_out), .clr(counter_2_ovf), .out(counter_2_out), .ovf(counter_2_ovf));
  PullDown pulldown_3 (.out(counter_2_ovf));
  DipSwitch dipswitch_4 (.out(dipswitch_1_out[8]));
  DipSwitch dipswitch_5 (.out(dipswitch_1_out[7]));
  DipSwitch dipswitch_6 (.out(dipswitch_1_out[6]));
  LED led_88 (.in(and_9_out));
  D_FF #(.Bits(12)) DATA (.D({DA3, DA2, DA1, DA0}), .C(DATA_CK), .Q(LATCHEDDATA));  // open: nQ
  LED led_89 (.in(i_hlt));
  DipSwitch dipswitch_7 (.out(dipswitch_1_out[5]));
  DipSwitch dipswitch_8 (.out(dipswitch_1_out[4]));
  DipSwitch dipswitch_9 (.out(dipswitch_1_out[3]));
  // Probe on LATCHEDDATA
  SEQUENCER sequencer_1 (
    .PH_FIRST(PH_FIRST), .PH_STB(PH_STB), .PH_LAST(PH_LAST),
    .STB_bits({STB9, STB8, STB7, STB6, STB5, STB4, STB3, STB2, STB1, STB0}),
    .CK_bits({CK9, CK8, CK7, CK6, CK5, CK4, CK3, CK2, CK1, CK0}), .CK_num(CK_NUM), .IN(counter_2_out));
  DipSwitch dipswitch_10 (.out(dipswitch_1_out[2]));
  DipSwitch dipswitch_11 (.out(dipswitch_1_out[1]));
  DipSwitch dipswitch_12 (.out(dipswitch_1_out[0]));
  // ROTATER rotater_1: pin names not known; wires that end beside it: {OPR_RIGHT, OPR_LEFT, OPR_X2}, add_2_s, xor_5_out, rotater_1_p4, rotater_1_p5
  LED led_90 (.in(IND2INC));
  assign driver_18_out = IND2INC ? {IND3, IND2, IND1, IND0} : 12'bz;  // Driver driver_18
  LED led_91 (.in(LD2INC));
  assign driver_18_out = LD2INC ? LATCHEDDATA : 12'bz;  // Driver driver_19
  // Probe on rotater_1_p4
  Seven_Seg_Hex seven_seg_hex_37 (.d(CK_NUM), .dp(1'b0));
  LED led_92 (.in(PH_FIRST));
  LED led_93 (.in(PH_STB));
  // Probe on driver_18_out
  Seven_Seg_Hex seven_seg_hex_38 (.d(CK_NUM), .dp(1'b0));
  LED led_94 (.in(PH_FIRST));
  LED led_95 (.in(PH_STB));
  Seven_Seg_Hex seven_seg_hex_39 (.d(CK_NUM), .dp(1'b0));
  LED led_96 (.in(PH_LAST));
  // Probe on INC_s
  Add #(.Bits(12)) INC (.a({12{1'b0}}), .b(driver_18_out), .c_i(1'b1), .s(INC_s), .c_o(INCZERO));
  LED led_97 (.in(PH_LAST));
  // Probe on LATCHED_PC
  LED led_98 (.in(PH_FIRST));
  LED led_99 (.in(PH_STB));
  LED led_100 (.in(PH_LAST));
  and and_10 (CNT_AND, AND, NOIND, CK1);
  LED led_101 (.in(CNT_AND));
  and and_11 (and_11_out, AND, NOIND, STB1);
  LED led_102 (.in(and_11_out));
  and and_12 (and_12_out, CK0, 1'b1, 1'b1);
  assign IR2RAMA = CNT_AND ? CNT_AND : 1'bz;  // Driver driver_20
  assign RAMD2AC_AND = CNT_AND ? CNT_AND : 1'bz;  // Driver driver_21
  assign RAM_OE = CNT_AND ? CNT_AND : 1'bz;  // Driver driver_22
  assign AC_CK = and_11_out ? and_11_out : 1'bz;  // Driver driver_23
  LED led_103 (.in(and_12_out));
  nor nor_1 (nor_1_out, AC[0], AC[1], AC[2], AC[3], AC[4], AC[5], AC[6], AC[7], AC[8], AC[9], AC[10], AC[11]);
  assign PC2ADDR = and_12_out ? and_12_out : 1'bz;  // Driver driver_24
  assign RAM_OE = and_12_out ? and_12_out : 1'bz;  // Driver driver_25
  assign IR_CK = and_12_out ? and_12_out : 1'bz;  // Driver driver_26
  assign PC_CK = and_12_out ? and_12_out : 1'bz;  // Driver driver_27
  LED led_104 (.in(nor_1_out));
  and and_13 (and_13_out, nor_1_out, OPR_SZASNA);
  and and_14 (and_14_out, AC[11], OPR_SMASPA);
  and and_15 (and_15_out, LINK, OPR_SNLSZL);
  and and_16 (CNT_AND_I, AND, IND, CK1);
  and and_17 (and_17_out, AND, IND, STB1);
  and and_18 (and_18_out, AND, IND, CK2);
  and and_19 (and_19_out, AND, IND, STB2);
  LED led_105 (.in(and_13_out));
  or or_6 (or_6_out, and_13_out, and_14_out, and_15_out);
  LED led_106 (.in(and_14_out));
  LED led_107 (.in(and_15_out));
  and and_20 (HALT, OPR_HLT, CK1);
  assign IR2RAMA = CNT_AND_I ? CNT_AND_I : 1'bz;  // Driver driver_28
  LED led_108 (.in(CNT_AND_I));
  assign RAMD2IND = CNT_AND_I ? CNT_AND_I : 1'bz;  // Driver driver_29
  assign RAM_OE = CNT_AND_I ? CNT_AND_I : 1'bz;  // Driver driver_30
  Driver driver_31 (.in(CNT_AND_I), .en(CNT_AND_I));  // open: out
  Driver driver_32 (.in(CNT_AND_I), .en(CNT_AND_I));  // open: out
  Driver driver_33 (.in(and_17_out), .en(and_17_out));  // open: out
  LED led_109 (.in(and_17_out));
  Driver driver_34 (.in(and_17_out), .en(and_17_out));  // open: out
  Driver driver_35 (.in(and_17_out), .en(and_17_out));  // open: out
  assign IND_CK = and_17_out ? and_17_out : 1'bz;  // Driver driver_36
  Driver driver_37 (.in(and_17_out), .en(and_17_out));  // open: out
  assign IND2RAMA = and_18_out ? and_18_out : 1'bz;  // Driver driver_38
  LED led_110 (.in(and_18_out));
  assign RAMD2AC_AND = and_18_out ? and_18_out : 1'bz;  // Driver driver_39
  assign RAM_OE = and_18_out ? and_18_out : 1'bz;  // Driver driver_40
  Driver driver_41 (.in(and_18_out), .en(and_18_out));  // open: out
  Driver driver_42 (.in(and_18_out), .en(and_18_out));  // open: out
  Driver driver_43 (.in(and_19_out), .en(and_19_out));  // open: out
  LED led_111 (.in(and_19_out));
  Driver driver_44 (.in(and_19_out), .en(and_19_out));  // open: out
  Driver driver_45 (.in(and_19_out), .en(and_19_out));  // open: out
  assign AC_CK = and_19_out ? and_19_out : 1'bz;  // Driver driver_46
  Driver driver_47 (.in(and_19_out), .en(and_19_out));  // open: out
  LED led_112 (.in(or_6_out));
  LED led_113 (.in(HALT));
  xor xor_7 (SKIP, or_6_out, OPR_TSTINV);
  LED led_114 (.in(SKIP));
  and and_21 (and_21_out, AND, AUTOIND, CK3);
  and and_22 (and_22_out, AND, AUTOIND, STB3);
  and and_23 (and_23_out, AND, AUTOIND, CK4);
  and and_24 (and_24_out, AND, AUTOIND, STB4);
  and and_25 (CNT_AND_IA, AND, AUTOIND, CK1);
  and and_26 (and_26_out, AND, AUTOIND, STB1);
  and and_27 (and_27_out, AND, AUTOIND, CK2);
  and and_28 (and_28_out, AND, AUTOIND, STB2);
  LED led_115 (.in(and_21_out));
  LED led_116 (.in(and_22_out));
  LED led_117 (.in(and_23_out));
  LED led_118 (.in(and_24_out));
  assign IR2RAMA = CNT_AND_IA ? CNT_AND_IA : 1'bz;  // Driver driver_48
  LED led_119 (.in(CNT_AND_IA));
  assign RAM_OE = CNT_AND_IA ? CNT_AND_IA : 1'bz;  // Driver driver_49
  assign IND2INC = CNT_AND_IA ? CNT_AND_IA : 1'bz;  // Driver driver_50
  LED led_120 (.in(and_26_out));
  assign IND_CK = and_26_out ? and_26_out : 1'bz;  // Driver driver_51
  assign INC2RAMD = and_27_out ? and_27_out : 1'bz;  // Driver driver_52
  LED led_121 (.in(and_27_out));
  assign IND2INC = and_27_out ? and_27_out : 1'bz;  // Driver driver_53
  assign IR2RAMA = and_27_out ? and_27_out : 1'bz;  // Driver driver_54
  LED led_122 (.in(and_28_out));
  assign RAM_WE = and_28_out ? and_28_out : 1'bz;  // Driver driver_55
  assign IR2RAMA = and_21_out ? and_21_out : 1'bz;  // Driver driver_56
  assign RAMD2IND = and_21_out ? and_21_out : 1'bz;  // Driver driver_57
  assign RAM_OE = and_21_out ? and_21_out : 1'bz;  // Driver driver_58
  Driver driver_59 (.in(and_21_out), .en(and_21_out));  // open: out
  Driver driver_60 (.in(and_21_out), .en(and_21_out));  // open: out
  Driver driver_61 (.in(and_22_out), .en(and_22_out));  // open: out
  Driver driver_62 (.in(and_22_out), .en(and_22_out));  // open: out
  Driver driver_63 (.in(and_22_out), .en(and_22_out));  // open: out
  assign IND_CK = and_22_out ? and_22_out : 1'bz;  // Driver driver_64
  Driver driver_65 (.in(and_22_out), .en(and_22_out));  // open: out
  assign IND2RAMA = and_23_out ? and_23_out : 1'bz;  // Driver driver_66
  assign RAMD2AC_AND = and_23_out ? and_23_out : 1'bz;  // Driver driver_67
  assign RAM_OE = and_23_out ? and_23_out : 1'bz;  // Driver driver_68
  Driver driver_69 (.in(and_23_out), .en(and_23_out));  // open: out
  Driver driver_70 (.in(and_23_out), .en(and_23_out));  // open: out
  Driver driver_71 (.in(and_24_out), .en(and_24_out));  // open: out
  Driver driver_72 (.in(and_24_out), .en(and_24_out));  // open: out
  Driver driver_73 (.in(and_24_out), .en(and_24_out));  // open: out
  assign AC_CK = and_24_out ? and_24_out : 1'bz;  // Driver driver_74
  Driver driver_75 (.in(and_24_out), .en(and_24_out));  // open: out
  or or_7 (or_7_out, INST_TPC, INST_TLS);
  and and_29 (and_29_out, INST_TSF, FLAG_PRNRDY, CK4);
  Monoflop #(.timerDelay(300)) monoflop_3 (.C(or_7_out), .R(1'b0), .Q(monoflop_3_q), .nQ(monoflop_3_nq));
  LED led_123 (.in(and_29_out));
  Counter #(.Bits(32)) COUNT (.en(1'b1), .C(or_7_out), .clr(1'b0), .out(COUNT_out));  // open: ovf
  Terminal #(.termWidth(20), .termHeight(10)) PRN (.D(AC[7:0]), .C(or_7_out), .en(1'b1));
  assign IR_CK = and_29_out ? and_29_out : 1'bz;  // Driver driver_76
  assign PC_CK = and_29_out ? and_29_out : 1'bz;  // Driver driver_77
  Driver driver_78 (.in(and_29_out), .en(and_29_out));  // open: out
  Driver driver_79 (.in(and_29_out), .en(and_29_out));  // open: out
  Driver driver_80 (.in(and_29_out), .en(and_29_out));  // open: out
  // Probe on COUNT_out
  and and_30 (CNT_TAD, TAD, NOIND, CK1);
  and and_31 (and_31_out, TAD, NOIND, STB1);
  Monoflop monoflop_4 (.C(monoflop_3_q), .R(1'b0), .Q(monoflop_4_q));  // open: nQ
  Monoflop monoflop_5 (.C(monoflop_3_nq), .R(1'b0), .Q(monoflop_5_q));  // open: nQ
  LED led_124 (.in(CNT_TAD));
  LED led_125 (.in(and_31_out));
  or or_8 (or_8_out, INST_TFL, monoflop_4_q);
  or or_9 (or_9_out, monoflop_5_q, INST_TCF);
  assign IR2RAMA = CNT_TAD ? CNT_TAD : 1'bz;  // Driver driver_81
  assign RAMD2AC_ADD = CNT_TAD ? CNT_TAD : 1'bz;  // Driver driver_82
  assign RAM_OE = CNT_TAD ? CNT_TAD : 1'bz;  // Driver driver_83
  assign driver_84_out = CNT_TAD ? CNT_TAD : 1'bz;  // Driver driver_84
  assign driver_85_out = CNT_TAD ? CNT_TAD : 1'bz;  // Driver driver_85
  Driver driver_86 (.in(and_31_out), .en(and_31_out));  // open: out
  Driver driver_87 (.in(and_31_out), .en(and_31_out));  // open: out
  Driver driver_88 (.in(and_31_out), .en(and_31_out));  // open: out
  assign AC_CK = and_31_out ? and_31_out : 1'bz;  // Driver driver_89
  assign LINK_CK = and_31_out ? and_31_out : 1'bz;  // Driver driver_90
  RS_FF_AS rs_ff_as_3 (.S(or_8_out), .R(or_9_out), .nQ(FLAG_PRNRDY));  // open: Q
  and and_32 (CNT_TAD_I, TAD, IND, CK1);
  and and_33 (and_33_out, TAD, IND, STB1);
  and and_34 (and_34_out, TAD, IND, CK2);
  and and_35 (and_35_out, TAD, IND, STB2);
  LED led_126 (.in(CNT_TAD_I));
  Driver driver_91 (.in(and_33_out), .en(and_33_out));  // open: out
  LED led_127 (.in(and_33_out));
  Driver driver_92 (.in(and_33_out), .en(and_33_out));  // open: out
  Driver driver_93 (.in(and_33_out), .en(and_33_out));  // open: out
  assign IND_CK = and_33_out ? and_33_out : 1'bz;  // Driver driver_94
  Driver driver_95 (.in(and_33_out), .en(and_33_out));  // open: out
  assign IND2RAMA = and_34_out ? and_34_out : 1'bz;  // Driver driver_96
  LED led_128 (.in(and_34_out));
  assign RAMD2AC_ADD = and_34_out ? and_34_out : 1'bz;  // Driver driver_97
  assign RAM_OE = and_34_out ? and_34_out : 1'bz;  // Driver driver_98
  Driver driver_99 (.in(and_34_out), .en(and_34_out));  // open: out
  Driver driver_100 (.in(and_34_out), .en(and_34_out));  // open: out
  Driver driver_101 (.in(and_35_out), .en(and_35_out));  // open: out
  LED led_129 (.in(and_35_out));
  Driver driver_102 (.in(and_35_out), .en(and_35_out));  // open: out
  Driver driver_103 (.in(and_35_out), .en(and_35_out));  // open: out
  assign AC_CK = and_35_out ? and_35_out : 1'bz;  // Driver driver_104
  assign LINK_CK = and_35_out ? and_35_out : 1'bz;  // Driver driver_105
  assign IR2RAMA = CNT_TAD_I ? CNT_TAD_I : 1'bz;  // Driver driver_106
  assign RAMD2IND = CNT_TAD_I ? CNT_TAD_I : 1'bz;  // Driver driver_107
  assign RAM_OE = CNT_TAD_I ? CNT_TAD_I : 1'bz;  // Driver driver_108
  Driver driver_109 (.in(CNT_TAD_I), .en(CNT_TAD_I));  // open: out
  Driver driver_110 (.in(CNT_TAD_I), .en(CNT_TAD_I));  // open: out
  and and_36 (CNT_TAD_IA, TAD, AUTOIND, CK1);
  and and_37 (and_37_out, TAD, AUTOIND, STB1);
  and and_38 (and_38_out, TAD, AUTOIND, CK2);
  and and_39 (and_39_out, TAD, AUTOIND, STB2);
  and and_40 (and_40_out, TAD, AUTOIND, CK3);
  and and_41 (and_41_out, TAD, AUTOIND, STB3);
  LED led_130 (.in(and_41_out));
  and and_42 (and_42_out, TAD, AUTOIND, CK4);
  LED led_131 (.in(and_42_out));
  and and_43 (and_43_out, TAD, AUTOIND, STB4);
  LED led_132 (.in(and_43_out));
  LED led_133 (.in(CNT_TAD_IA));
  LED led_134 (.in(and_37_out));
  LED led_135 (.in(and_38_out));
  LED led_136 (.in(and_39_out));
  assign IR2RAMA = and_40_out ? and_40_out : 1'bz;  // Driver driver_111
  LED led_137 (.in(and_40_out));
  assign RAMD2IND = and_40_out ? and_40_out : 1'bz;  // Driver driver_112
  assign RAM_OE = and_40_out ? and_40_out : 1'bz;  // Driver driver_113
  Driver driver_114 (.in(and_40_out), .en(and_40_out));  // open: out
  Driver driver_115 (.in(and_40_out), .en(and_40_out));  // open: out
  Driver driver_116 (.in(and_41_out), .en(and_41_out));  // open: out
  Driver driver_117 (.in(and_41_out), .en(and_41_out));  // open: out
  Driver driver_118 (.in(and_41_out), .en(and_41_out));  // open: out
  assign IND_CK = and_41_out ? and_41_out : 1'bz;  // Driver driver_119
  Driver driver_120 (.in(and_41_out), .en(and_41_out));  // open: out
  assign IND2RAMA = and_42_out ? and_42_out : 1'bz;  // Driver driver_121
  assign RAMD2AC_ADD = and_42_out ? and_42_out : 1'bz;  // Driver driver_122
  assign RAM_OE = and_42_out ? and_42_out : 1'bz;  // Driver driver_123
  Driver driver_124 (.in(and_42_out), .en(and_42_out));  // open: out
  Driver driver_125 (.in(and_42_out), .en(and_42_out));  // open: out
  Driver driver_126 (.in(and_43_out), .en(and_43_out));  // open: out
  Driver driver_127 (.in(and_43_out), .en(and_43_out));  // open: out
  Driver driver_128 (.in(and_43_out), .en(and_43_out));  // open: out
  assign AC_CK = and_43_out ? and_43_out : 1'bz;  // Driver driver_129
  assign LINK_CK = and_43_out ? and_43_out : 1'bz;  // Driver driver_130
  assign IR2RAMA = CNT_TAD_IA ? CNT_TAD_IA : 1'bz;  // Driver driver_131
  assign RAM_OE = CNT_TAD_IA ? CNT_TAD_IA : 1'bz;  // Driver driver_132
  assign IND2INC = CNT_TAD_IA ? CNT_TAD_IA : 1'bz;  // Driver driver_133
  assign IND_CK = and_37_out ? and_37_out : 1'bz;  // Driver driver_134
  assign INC2RAMD = and_38_out ? and_38_out : 1'bz;  // Driver driver_135
  assign IND2INC = and_38_out ? and_38_out : 1'bz;  // Driver driver_136
  assign IR2RAMA = and_38_out ? and_38_out : 1'bz;  // Driver driver_137
  assign RAM_WE = and_39_out ? and_39_out : 1'bz;  // Driver driver_138
  and and_44 (CNT_ISZ, ISZ, NOIND, CK1);
  and and_45 (and_45_out, ISZ, NOIND, STB1);
  and and_46 (and_46_out, ISZ, NOIND, CK2);
  and and_47 (and_47_out, ISZ, NOIND, CK3);
  and and_48 (and_48_out, ISZ, NOIND, INCZERO, CK4);
  LED led_138 (.in(CNT_ISZ));
  LED led_139 (.in(and_45_out));
  LED led_140 (.in(and_46_out));
  LED led_141 (.in(and_47_out));
  LED led_142 (.in(and_48_out));
  assign IR2RAMA = CNT_ISZ ? CNT_ISZ : 1'bz;  // Driver driver_139
  assign RAM_OE = CNT_ISZ ? CNT_ISZ : 1'bz;  // Driver driver_140
  Driver driver_141 (.in(CNT_ISZ), .en(CNT_ISZ));  // open: out
  Driver driver_142 (.in(CNT_ISZ), .en(CNT_ISZ));  // open: out
  Driver driver_143 (.in(CNT_ISZ), .en(CNT_ISZ));  // open: out
  Driver driver_144 (.in(and_45_out), .en(and_45_out));  // open: out
  Driver driver_145 (.in(and_45_out), .en(and_45_out));  // open: out
  assign DATA_CK = and_45_out ? and_45_out : 1'bz;  // Driver driver_146
  assign LD2INC = and_45_out ? and_45_out : 1'bz;  // Driver driver_147
  Driver driver_148 (.in(and_45_out), .en(and_45_out));  // open: out
  assign IR2RAMA = and_46_out ? and_46_out : 1'bz;  // Driver driver_149
  assign RAM_WE = and_46_out ? and_46_out : 1'bz;  // Driver driver_150
  assign INC2RAMD = and_46_out ? and_46_out : 1'bz;  // Driver driver_151
  assign LD2INC = and_46_out ? and_46_out : 1'bz;  // Driver driver_152
  Driver driver_153 (.in(and_46_out), .en(and_46_out));  // open: out
  assign IR2RAMA = and_47_out ? and_47_out : 1'bz;  // Driver driver_154
  assign RAM_OE = and_47_out ? and_47_out : 1'bz;  // Driver driver_155
  assign LD2INC = and_47_out ? and_47_out : 1'bz;  // Driver driver_156
  Driver driver_157 (.in(and_47_out), .en(and_47_out));  // open: out
  Driver driver_158 (.in(and_47_out), .en(and_47_out));  // open: out
  assign PC_CK = and_48_out ? and_48_out : 1'bz;  // Driver driver_159
  assign LD2INC = and_48_out ? and_48_out : 1'bz;  // Driver driver_160
  Driver driver_161 (.in(and_48_out), .en(and_48_out));  // open: out
  Driver driver_162 (.in(and_48_out), .en(and_48_out));  // open: out
  Driver driver_163 (.in(and_48_out), .en(and_48_out));  // open: out
  and and_49 (CNT_ISZ_I, ISZ, IND, CK1);
  LED led_143 (.in(CNT_ISZ_I));
  and and_50 (and_50_out, ISZ, IND, STB1);
  LED led_144 (.in(and_50_out));
  and and_51 (and_51_out, ISZ, IND, CK2);
  LED led_145 (.in(and_51_out));
  and and_52 (and_52_out, ISZ, IND, STB2);
  LED led_146 (.in(and_52_out));
  and and_53 (and_53_out, ISZ, IND, CK3);
  LED led_147 (.in(and_53_out));
  and and_54 (and_54_out, ISZ, IND, CK4);
  LED led_148 (.in(and_54_out));
  and and_55 (and_55_out, ISZ, IND, INCZERO, CK5);
  LED led_149 (.in(and_55_out));
  assign IR2RAMA = CNT_ISZ_I ? CNT_ISZ_I : 1'bz;  // Driver driver_164
  assign RAMD2IND = CNT_ISZ_I ? CNT_ISZ_I : 1'bz;  // Driver driver_165
  assign RAM_OE = CNT_ISZ_I ? CNT_ISZ_I : 1'bz;  // Driver driver_166
  Driver driver_167 (.in(CNT_ISZ_I), .en(CNT_ISZ_I));  // open: out
  Driver driver_168 (.in(CNT_ISZ_I), .en(CNT_ISZ_I));  // open: out
  Driver driver_169 (.in(and_50_out), .en(and_50_out));  // open: out
  Driver driver_170 (.in(and_50_out), .en(and_50_out));  // open: out
  Driver driver_171 (.in(and_50_out), .en(and_50_out));  // open: out
  assign IND_CK = and_50_out ? and_50_out : 1'bz;  // Driver driver_172
  Driver driver_173 (.in(and_50_out), .en(and_50_out));  // open: out
  assign IND2RAMA = and_51_out ? and_51_out : 1'bz;  // Driver driver_174
  assign RAM_OE = and_51_out ? and_51_out : 1'bz;  // Driver driver_175
  Driver driver_176 (.in(and_51_out), .en(and_51_out));  // open: out
  Driver driver_177 (.in(and_51_out), .en(and_51_out));  // open: out
  Driver driver_178 (.in(and_51_out), .en(and_51_out));  // open: out
  Driver driver_179 (.in(and_52_out), .en(and_52_out));  // open: out
  Driver driver_180 (.in(and_52_out), .en(and_52_out));  // open: out
  assign DATA_CK = and_52_out ? and_52_out : 1'bz;  // Driver driver_181
  assign LD2INC = and_52_out ? and_52_out : 1'bz;  // Driver driver_182
  Driver driver_183 (.in(and_52_out), .en(and_52_out));  // open: out
  assign IND2RAMA = and_53_out ? and_53_out : 1'bz;  // Driver driver_184
  assign RAM_WE = and_53_out ? and_53_out : 1'bz;  // Driver driver_185
  assign INC2RAMD = and_53_out ? and_53_out : 1'bz;  // Driver driver_186
  assign LD2INC = and_53_out ? and_53_out : 1'bz;  // Driver driver_187
  Driver driver_188 (.in(and_53_out), .en(and_53_out));  // open: out
  assign IND2RAMA = and_54_out ? and_54_out : 1'bz;  // Driver driver_189
  assign RAM_OE = and_54_out ? and_54_out : 1'bz;  // Driver driver_190
  assign LD2INC = and_54_out ? and_54_out : 1'bz;  // Driver driver_191
  Driver driver_192 (.in(and_54_out), .en(and_54_out));  // open: out
  Driver driver_193 (.in(and_54_out), .en(and_54_out));  // open: out
  assign PC_CK = and_55_out ? and_55_out : 1'bz;  // Driver driver_194
  assign LD2INC = and_55_out ? and_55_out : 1'bz;  // Driver driver_195
  Driver driver_196 (.in(and_55_out), .en(and_55_out));  // open: out
  Driver driver_197 (.in(and_55_out), .en(and_55_out));  // open: out
  Driver driver_198 (.in(and_55_out), .en(and_55_out));  // open: out
  and and_56 (and_56_out, ISZ, AUTOIND, CK3);
  and and_57 (and_57_out, ISZ, AUTOIND, STB3);
  and and_58 (and_58_out, ISZ, AUTOIND, CK4);
  and and_59 (and_59_out, ISZ, AUTOIND, STB4);
  and and_60 (and_60_out, ISZ, AUTOIND, CK5);
  and and_61 (and_61_out, ISZ, AUTOIND, CK6);
  and and_62 (and_62_out, ISZ, AUTOIND, INCZERO, CK7);
  and and_63 (CNT_ISZ_IA, ISZ, AUTOIND, CK1);
  and and_64 (and_64_out, ISZ, AUTOIND, STB1);
  and and_65 (and_65_out, ISZ, AUTOIND, CK2);
  and and_66 (and_66_out, ISZ, AUTOIND, STB2);
  LED led_150 (.in(and_56_out));
  LED led_151 (.in(and_57_out));
  LED led_152 (.in(and_58_out));
  LED led_153 (.in(and_59_out));
  assign IND2RAMA = and_60_out ? and_60_out : 1'bz;  // Driver driver_199
  LED led_154 (.in(and_60_out));
  assign RAM_WE = and_60_out ? and_60_out : 1'bz;  // Driver driver_200
  assign INC2RAMD = and_60_out ? and_60_out : 1'bz;  // Driver driver_201
  assign LD2INC = and_60_out ? and_60_out : 1'bz;  // Driver driver_202
  Driver driver_203 (.in(and_60_out), .en(and_60_out));  // open: out
  assign IND2RAMA = and_61_out ? and_61_out : 1'bz;  // Driver driver_204
  LED led_155 (.in(and_61_out));
  assign RAM_OE = and_61_out ? and_61_out : 1'bz;  // Driver driver_205
  assign LD2INC = and_61_out ? and_61_out : 1'bz;  // Driver driver_206
  Driver driver_207 (.in(and_61_out), .en(and_61_out));  // open: out
  Driver driver_208 (.in(and_61_out), .en(and_61_out));  // open: out
  assign PC_CK = and_62_out ? and_62_out : 1'bz;  // Driver driver_209
  LED led_156 (.in(and_62_out));
  assign LD2INC = and_62_out ? and_62_out : 1'bz;  // Driver driver_210
  Driver driver_211 (.in(and_62_out), .en(and_62_out));  // open: out
  Driver driver_212 (.in(and_62_out), .en(and_62_out));  // open: out
  Driver driver_213 (.in(and_62_out), .en(and_62_out));  // open: out
  LED led_157 (.in(CNT_ISZ_IA));
  LED led_158 (.in(and_64_out));
  LED led_159 (.in(and_65_out));
  LED led_160 (.in(and_66_out));
  assign IR2RAMA = and_56_out ? and_56_out : 1'bz;  // Driver driver_214
  assign RAMD2IND = and_56_out ? and_56_out : 1'bz;  // Driver driver_215
  assign RAM_OE = and_56_out ? and_56_out : 1'bz;  // Driver driver_216
  Driver driver_217 (.in(and_56_out), .en(and_56_out));  // open: out
  Driver driver_218 (.in(and_56_out), .en(and_56_out));  // open: out
  Driver driver_219 (.in(and_57_out), .en(and_57_out));  // open: out
  Driver driver_220 (.in(and_57_out), .en(and_57_out));  // open: out
  Driver driver_221 (.in(and_57_out), .en(and_57_out));  // open: out
  assign IND_CK = and_57_out ? and_57_out : 1'bz;  // Driver driver_222
  Driver driver_223 (.in(and_57_out), .en(and_57_out));  // open: out
  assign IND2RAMA = and_58_out ? and_58_out : 1'bz;  // Driver driver_224
  assign RAM_OE = and_58_out ? and_58_out : 1'bz;  // Driver driver_225
  Driver driver_226 (.in(and_58_out), .en(and_58_out));  // open: out
  Driver driver_227 (.in(and_58_out), .en(and_58_out));  // open: out
  Driver driver_228 (.in(and_58_out), .en(and_58_out));  // open: out
  assign IND2RAMA = and_59_out ? and_59_out : 1'bz;  // Driver driver_229
  assign RAM_OE = and_59_out ? and_59_out : 1'bz;  // Driver driver_230
  assign DATA_CK = and_59_out ? and_59_out : 1'bz;  // Driver driver_231
  assign LD2INC = and_59_out ? and_59_out : 1'bz;  // Driver driver_232
  Driver driver_233 (.in(and_59_out), .en(and_59_out));  // open: out
  assign IR2RAMA = CNT_ISZ_IA ? CNT_ISZ_IA : 1'bz;  // Driver driver_234
  assign RAM_OE = CNT_ISZ_IA ? CNT_ISZ_IA : 1'bz;  // Driver driver_235
  assign IND2INC = CNT_ISZ_IA ? CNT_ISZ_IA : 1'bz;  // Driver driver_236
  assign IND_CK = and_64_out ? and_64_out : 1'bz;  // Driver driver_237
  assign INC2RAMD = and_65_out ? and_65_out : 1'bz;  // Driver driver_238
  assign IND2INC = and_65_out ? and_65_out : 1'bz;  // Driver driver_239
  assign IR2RAMA = and_65_out ? and_65_out : 1'bz;  // Driver driver_240
  assign RAM_WE = and_66_out ? and_66_out : 1'bz;  // Driver driver_241
  and and_67 (CNT_DCA, DCA, NOIND, CK1);
  LED led_161 (.in(CNT_DCA));
  and and_68 (and_68_out, DCA, DCA, STB1);
  LED led_162 (.in(and_68_out));
  and and_69 (and_69_out, DCA, DCA, CK2);
  LED led_163 (.in(and_69_out));
  assign IR2RAMA = CNT_DCA ? CNT_DCA : 1'bz;  // Driver driver_242
  assign AC2RAMD = CNT_DCA ? CNT_DCA : 1'bz;  // Driver driver_243
  Driver driver_244 (.in(CNT_DCA), .en(CNT_DCA));  // open: out
  Driver driver_245 (.in(CNT_DCA), .en(CNT_DCA));  // open: out
  Driver driver_246 (.in(CNT_DCA), .en(CNT_DCA));  // open: out
  Driver driver_247 (.in(and_68_out), .en(and_68_out));  // open: out
  Driver driver_248 (.in(and_68_out), .en(and_68_out));  // open: out
  assign RAM_WE = and_68_out ? and_68_out : 1'bz;  // Driver driver_249
  assign CLA = and_68_out ? and_68_out : 1'bz;  // Driver driver_250
  Driver driver_251 (.in(and_68_out), .en(and_68_out));  // open: out
  assign CLAx = and_69_out ? and_69_out : 1'bz;  // Driver driver_252
  assign ROT2AC = and_69_out ? and_69_out : 1'bz;  // Driver driver_253
  assign AC_CK = and_69_out ? and_69_out : 1'bz;  // Driver driver_254
  Driver driver_255 (.in(and_69_out), .en(and_69_out));  // open: out
  Driver driver_256 (.in(and_69_out), .en(and_69_out));  // open: out
  and and_70 (CNT_DCA_I, DCA, IND, CK1);
  and and_71 (and_71_out, DCA, IND, STB1);
  and and_72 (and_72_out, DCA, IND, CK2);
  and and_73 (and_73_out, DCA, IND, STB2);
  and and_74 (and_74_out, DCA, IND, CK3);
  LED led_164 (.in(CNT_DCA_I));
  LED led_165 (.in(and_71_out));
  LED led_166 (.in(and_72_out));
  LED led_167 (.in(and_73_out));
  LED led_168 (.in(and_74_out));
  assign IR2RAMA = CNT_DCA_I ? CNT_DCA_I : 1'bz;  // Driver driver_257
  assign RAMD2IND = CNT_DCA_I ? CNT_DCA_I : 1'bz;  // Driver driver_258
  assign RAM_OE = CNT_DCA_I ? CNT_DCA_I : 1'bz;  // Driver driver_259
  assign driver_260_out = CNT_DCA_I ? CNT_DCA_I : 1'bz;  // Driver driver_260
  assign driver_261_out = CNT_DCA_I ? CNT_DCA_I : 1'bz;  // Driver driver_261
  assign IR2RAMA = and_71_out ? and_71_out : 1'bz;  // Driver driver_262
  assign RAMD2IND = and_71_out ? and_71_out : 1'bz;  // Driver driver_263
  assign RAM_OE = and_71_out ? and_71_out : 1'bz;  // Driver driver_264
  assign IND_CK = and_71_out ? and_71_out : 1'bz;  // Driver driver_265
  assign driver_266_out = and_71_out ? and_71_out : 1'bz;  // Driver driver_266
  assign IND2RAMA = and_72_out ? and_72_out : 1'bz;  // Driver driver_267
  assign AC2RAMD = and_72_out ? and_72_out : 1'bz;  // Driver driver_268
  Driver driver_269 (.in(and_72_out), .en(and_72_out));  // open: out
  Driver driver_270 (.in(and_72_out), .en(and_72_out));  // open: out
  Driver driver_271 (.in(and_72_out), .en(and_72_out));  // open: out
  Driver driver_272 (.in(and_73_out), .en(and_73_out));  // open: out
  Driver driver_273 (.in(and_73_out), .en(and_73_out));  // open: out
  assign RAM_WE = and_73_out ? and_73_out : 1'bz;  // Driver driver_274
  assign CLA = and_73_out ? and_73_out : 1'bz;  // Driver driver_275
  Driver driver_276 (.in(and_73_out), .en(and_73_out));  // open: out
  assign CLAx = and_74_out ? and_74_out : 1'bz;  // Driver driver_277
  assign ROT2AC = and_74_out ? and_74_out : 1'bz;  // Driver driver_278
  assign AC_CK = and_74_out ? and_74_out : 1'bz;  // Driver driver_279
  Driver driver_280 (.in(and_74_out), .en(and_74_out));  // open: out
  Driver driver_281 (.in(and_74_out), .en(and_74_out));  // open: out
  and and_75 (CNT_DCA_IA, DCA, AUTOIND, CK1);
  and and_76 (and_76_out, DCA, AUTOIND, STB1);
  and and_77 (and_77_out, DCA, AUTOIND, CK2);
  and and_78 (and_78_out, DCA, AUTOIND, STB2);
  and and_79 (and_79_out, DCA, AUTOIND, CK3);
  and and_80 (and_80_out, DCA, AUTOIND, STB3);
  and and_81 (and_81_out, DCA, AUTOIND, CK4);
  LED led_169 (.in(and_81_out));
  and and_82 (and_82_out, DCA, AUTOIND, STB4);
  LED led_170 (.in(and_82_out));
  and and_83 (and_83_out, DCA, AUTOIND, CK5);
  LED led_171 (.in(and_83_out));
  LED led_172 (.in(CNT_DCA_IA));
  LED led_173 (.in(and_76_out));
  LED led_174 (.in(and_77_out));
  LED led_175 (.in(and_78_out));
  assign IR2RAMA = and_79_out ? and_79_out : 1'bz;  // Driver driver_282
  LED led_176 (.in(and_79_out));
  assign RAMD2IND = and_79_out ? and_79_out : 1'bz;  // Driver driver_283
  assign RAM_OE = and_79_out ? and_79_out : 1'bz;  // Driver driver_284
  assign driver_285_out = and_79_out ? and_79_out : 1'bz;  // Driver driver_285
  assign driver_286_out = and_79_out ? and_79_out : 1'bz;  // Driver driver_286
  Driver driver_287 (.in(and_80_out), .en(and_80_out));  // open: out
  LED led_177 (.in(and_80_out));
  Driver driver_288 (.in(and_80_out), .en(and_80_out));  // open: out
  Driver driver_289 (.in(and_80_out), .en(and_80_out));  // open: out
  assign IND_CK = and_80_out ? and_80_out : 1'bz;  // Driver driver_290
  assign driver_291_out = and_80_out ? and_80_out : 1'bz;  // Driver driver_291
  assign IND2RAMA = and_81_out ? and_81_out : 1'bz;  // Driver driver_292
  assign AC2RAMD = and_81_out ? and_81_out : 1'bz;  // Driver driver_293
  Driver driver_294 (.in(and_81_out), .en(and_81_out));  // open: out
  Driver driver_295 (.in(and_81_out), .en(and_81_out));  // open: out
  Driver driver_296 (.in(and_81_out), .en(and_81_out));  // open: out
  Driver driver_297 (.in(and_82_out), .en(and_82_out));  // open: out
  Driver driver_298 (.in(and_82_out), .en(and_82_out));  // open: out
  assign RAM_WE = and_82_out ? and_82_out : 1'bz;  // Driver driver_299
  assign CLA = and_82_out ? and_82_out : 1'bz;  // Driver driver_300
  Driver driver_301 (.in(and_82_out), .en(and_82_out));  // open: out
  assign CLAx = and_83_out ? and_83_out : 1'bz;  // Driver driver_302
  assign ROT2AC = and_83_out ? and_83_out : 1'bz;  // Driver driver_303
  assign AC_CK = and_83_out ? and_83_out : 1'bz;  // Driver driver_304
  Driver driver_305 (.in(and_83_out), .en(and_83_out));  // open: out
  Driver driver_306 (.in(and_83_out), .en(and_83_out));  // open: out
  assign IR2RAMA = CNT_DCA_IA ? CNT_DCA_IA : 1'bz;  // Driver driver_307
  assign RAM_OE = CNT_DCA_IA ? CNT_DCA_IA : 1'bz;  // Driver driver_308
  assign IND2INC = CNT_DCA_IA ? CNT_DCA_IA : 1'bz;  // Driver driver_309
  assign IND_CK = and_76_out ? and_76_out : 1'bz;  // Driver driver_310
  assign INC2RAMD = and_77_out ? and_77_out : 1'bz;  // Driver driver_311
  assign IND2INC = and_77_out ? and_77_out : 1'bz;  // Driver driver_312
  assign IR2RAMA = and_77_out ? and_77_out : 1'bz;  // Driver driver_313
  assign RAM_WE = and_78_out ? and_78_out : 1'bz;  // Driver driver_314
  and and_84 (CNT_JMS, JMS, NOIND, CK1);
  and and_85 (and_85_out, JMS, NOIND, STB1);
  and and_86 (and_86_out, JMS, NOIND, CK2);
  and and_87 (and_87_out, JMS, NOIND, CK3);
  and and_88 (and_88_out, JMS, NOIND, CK4);
  LED led_178 (.in(CNT_JMS));
  Driver driver_315 (.in(and_85_out), .en(and_85_out));  // open: out
  LED led_179 (.in(and_85_out));
  Driver driver_316 (.in(and_85_out), .en(and_85_out));  // open: out
  assign RAM_WE = and_85_out ? and_85_out : 1'bz;  // Driver driver_317
  assign IR2PC = and_85_out ? and_85_out : 1'bz;  // Driver driver_318
  assign driver_319_out = and_85_out ? and_85_out : 1'bz;  // Driver driver_319
  LED led_180 (.in(and_86_out));
  LED led_181 (.in(and_87_out));
  LED led_182 (.in(and_88_out));
  assign PC2RAMD = CNT_JMS ? CNT_JMS : 1'bz;  // Driver driver_320
  assign IR2RAMA = CNT_JMS ? CNT_JMS : 1'bz;  // Driver driver_321
  assign driver_322_out = CNT_JMS ? CNT_JMS : 1'bz;  // Driver driver_322
  assign driver_323_out = CNT_JMS ? CNT_JMS : 1'bz;  // Driver driver_323
  assign driver_324_out = CNT_JMS ? CNT_JMS : 1'bz;  // Driver driver_324
  assign IR2PC = and_86_out ? and_86_out : 1'bz;  // Driver driver_325
  assign PC_LD = and_86_out ? and_86_out : 1'bz;  // Driver driver_326
  assign PC_CK = and_86_out ? and_86_out : 1'bz;  // Driver driver_327
  assign driver_328_out = and_86_out ? and_86_out : 1'bz;  // Driver driver_328
  assign driver_329_out = and_86_out ? and_86_out : 1'bz;  // Driver driver_329
  assign driver_330_out = and_87_out ? and_87_out : 1'bz;  // Driver driver_330
  assign driver_331_out = and_87_out ? and_87_out : 1'bz;  // Driver driver_331
  assign driver_332_out = and_87_out ? and_87_out : 1'bz;  // Driver driver_332
  assign driver_333_out = and_87_out ? and_87_out : 1'bz;  // Driver driver_333
  assign driver_334_out = and_87_out ? and_87_out : 1'bz;  // Driver driver_334
  assign PC_CK = and_88_out ? and_88_out : 1'bz;  // Driver driver_335
  assign driver_336_out = and_88_out ? and_88_out : 1'bz;  // Driver driver_336
  assign driver_337_out = and_88_out ? and_88_out : 1'bz;  // Driver driver_337
  assign driver_338_out = and_88_out ? and_88_out : 1'bz;  // Driver driver_338
  Driver driver_339 (.in(and_88_out), .en(and_88_out));  // open: out
  and and_89 (CNT_JMS_I, JMS, IND, CK1);
  and and_90 (and_90_out, JMS, IND, STB1);
  and and_91 (and_91_out, JMS, IND, CK2);
  and and_92 (and_92_out, JMS, IND, CK3);
  and and_93 (and_93_out, JMS, IND, CK4);
  and and_94 (and_94_out, JMS, IND, CK5);
  and and_95 (and_95_out, JMS, IND, CK6);
  LED led_183 (.in(CNT_JMS_I));
  LED led_184 (.in(and_90_out));
  LED led_185 (.in(and_91_out));
  LED led_186 (.in(and_92_out));
  LED led_187 (.in(and_93_out));
  LED led_188 (.in(and_94_out));
  LED led_189 (.in(and_95_out));
  assign IR2RAMA = CNT_JMS_I ? CNT_JMS_I : 1'bz;  // Driver driver_340
  assign RAMD2IND = CNT_JMS_I ? CNT_JMS_I : 1'bz;  // Driver driver_341
  assign RAM_OE = CNT_JMS_I ? CNT_JMS_I : 1'bz;  // Driver driver_342
  assign driver_343_out = CNT_JMS_I ? CNT_JMS_I : 1'bz;  // Driver driver_343
  assign driver_344_out = CNT_JMS_I ? CNT_JMS_I : 1'bz;  // Driver driver_344
  Driver driver_345 (.in(and_90_out), .en(and_90_out));  // open: out
  Driver driver_346 (.in(and_90_out), .en(and_90_out));  // open: out
  Driver driver_347 (.in(and_90_out), .en(and_90_out));  // open: out
  assign IND_CK = and_90_out ? and_90_out : 1'bz;  // Driver driver_348
  assign driver_349_out = and_90_out ? and_90_out : 1'bz;  // Driver driver_349
  assign IND2RAMA = and_91_out ? and_91_out : 1'bz;  // Driver driver_350
  assign PC2RAMD = and_91_out ? and_91_out : 1'bz;  // Driver driver_351
  Driver driver_352 (.in(and_91_out), .en(and_91_out));  // open: out
  assign driver_353_out = and_91_out ? and_91_out : 1'bz;  // Driver driver_353
  assign driver_354_out = and_91_out ? and_91_out : 1'bz;  // Driver driver_354
  assign IND2RAMA = and_92_out ? and_92_out : 1'bz;  // Driver driver_355
  assign PC2RAMD = and_92_out ? and_92_out : 1'bz;  // Driver driver_356
  assign RAM_WE = and_92_out ? and_92_out : 1'bz;  // Driver driver_357
  assign PC_LD = and_92_out ? and_92_out : 1'bz;  // Driver driver_358
  assign IND2PC = and_92_out ? and_92_out : 1'bz;  // Driver driver_359
  assign IND2PC = and_93_out ? and_93_out : 1'bz;  // Driver driver_360
  assign PC_LD = and_93_out ? and_93_out : 1'bz;  // Driver driver_361
  assign PC_CK = and_93_out ? and_93_out : 1'bz;  // Driver driver_362
  Driver driver_363 (.in(and_93_out), .en(and_93_out));  // open: out
  assign driver_364_out = and_93_out ? and_93_out : 1'bz;  // Driver driver_364
  assign IND2PC = and_94_out ? and_94_out : 1'bz;  // Driver driver_365
  assign PC_LD = and_94_out ? and_94_out : 1'bz;  // Driver driver_366
  assign driver_367_out = and_94_out ? and_94_out : 1'bz;  // Driver driver_367
  assign driver_368_out = and_94_out ? and_94_out : 1'bz;  // Driver driver_368
  assign driver_369_out = and_94_out ? and_94_out : 1'bz;  // Driver driver_369
  assign PC_CK = and_95_out ? and_95_out : 1'bz;  // Driver driver_370
  assign driver_371_out = and_95_out ? and_95_out : 1'bz;  // Driver driver_371
  assign driver_372_out = and_95_out ? and_95_out : 1'bz;  // Driver driver_372
  assign driver_373_out = and_95_out ? and_95_out : 1'bz;  // Driver driver_373
  Driver driver_374 (.in(and_95_out), .en(and_95_out));  // open: out
  and and_96 (and_96_out, JMS, AUTOIND, CK3);
  and and_97 (and_97_out, JMS, AUTOIND, STB3);
  and and_98 (and_98_out, JMS, AUTOIND, CK4);
  and and_99 (and_99_out, JMS, AUTOIND, CK5);
  and and_100 (and_100_out, JMS, AUTOIND, CK6);
  and and_101 (and_101_out, JMS, AUTOIND, CK7);
  and and_102 (and_102_out, JMS, AUTOIND, CK8);
  and and_103 (CNT_JMS_IA, JMS, AUTOIND, CK1);
  and and_104 (and_104_out, JMS, AUTOIND, STB1);
  and and_105 (and_105_out, JMS, AUTOIND, CK2);
  and and_106 (and_106_out, JMS, AUTOIND, STB2);
  LED led_190 (.in(and_96_out));
  LED led_191 (.in(and_97_out));
  LED led_192 (.in(and_98_out));
  LED led_193 (.in(and_99_out));
  LED led_194 (.in(and_100_out));
  LED led_195 (.in(and_101_out));
  LED led_196 (.in(and_102_out));
  assign IR2RAMA = CNT_JMS_IA ? CNT_JMS_IA : 1'bz;  // Driver driver_375
  LED led_197 (.in(CNT_JMS_IA));
  assign RAM_OE = CNT_JMS_IA ? CNT_JMS_IA : 1'bz;  // Driver driver_376
  assign IND2INC = CNT_JMS_IA ? CNT_JMS_IA : 1'bz;  // Driver driver_377
  LED led_198 (.in(and_104_out));
  assign IND_CK = and_104_out ? and_104_out : 1'bz;  // Driver driver_378
  assign INC2RAMD = and_105_out ? and_105_out : 1'bz;  // Driver driver_379
  LED led_199 (.in(and_105_out));
  assign IND2INC = and_105_out ? and_105_out : 1'bz;  // Driver driver_380
  assign IR2RAMA = and_105_out ? and_105_out : 1'bz;  // Driver driver_381
  LED led_200 (.in(and_106_out));
  assign RAM_WE = and_106_out ? and_106_out : 1'bz;  // Driver driver_382
  assign IR2RAMA = and_96_out ? and_96_out : 1'bz;  // Driver driver_383
  assign RAMD2IND = and_96_out ? and_96_out : 1'bz;  // Driver driver_384
  assign RAM_OE = and_96_out ? and_96_out : 1'bz;  // Driver driver_385
  assign driver_386_out = and_96_out ? and_96_out : 1'bz;  // Driver driver_386
  assign driver_387_out = and_96_out ? and_96_out : 1'bz;  // Driver driver_387
  Driver driver_388 (.in(and_97_out), .en(and_97_out));  // open: out
  Driver driver_389 (.in(and_97_out), .en(and_97_out));  // open: out
  Driver driver_390 (.in(and_97_out), .en(and_97_out));  // open: out
  assign IND_CK = and_97_out ? and_97_out : 1'bz;  // Driver driver_391
  assign driver_392_out = and_97_out ? and_97_out : 1'bz;  // Driver driver_392
  assign IND2RAMA = and_98_out ? and_98_out : 1'bz;  // Driver driver_393
  assign PC2RAMD = and_98_out ? and_98_out : 1'bz;  // Driver driver_394
  Driver driver_395 (.in(and_98_out), .en(and_98_out));  // open: out
  assign driver_396_out = and_98_out ? and_98_out : 1'bz;  // Driver driver_396
  assign driver_397_out = and_98_out ? and_98_out : 1'bz;  // Driver driver_397
  assign IND2RAMA = and_99_out ? and_99_out : 1'bz;  // Driver driver_398
  assign PC2RAMD = and_99_out ? and_99_out : 1'bz;  // Driver driver_399
  assign RAM_WE = and_99_out ? and_99_out : 1'bz;  // Driver driver_400
  assign PC_LD = and_99_out ? and_99_out : 1'bz;  // Driver driver_401
  assign IND2PC = and_99_out ? and_99_out : 1'bz;  // Driver driver_402
  assign IND2PC = and_100_out ? and_100_out : 1'bz;  // Driver driver_403
  assign PC_LD = and_100_out ? and_100_out : 1'bz;  // Driver driver_404
  assign PC_CK = and_100_out ? and_100_out : 1'bz;  // Driver driver_405
  Driver driver_406 (.in(and_100_out), .en(and_100_out));  // open: out
  assign driver_407_out = and_100_out ? and_100_out : 1'bz;  // Driver driver_407
  Driver driver_408 (.in(and_101_out), .en(and_101_out));  // open: out
  Driver driver_409 (.in(and_101_out), .en(and_101_out));  // open: out
  assign driver_410_out = and_101_out ? and_101_out : 1'bz;  // Driver driver_410
  assign driver_411_out = and_101_out ? and_101_out : 1'bz;  // Driver driver_411
  assign driver_412_out = and_101_out ? and_101_out : 1'bz;  // Driver driver_412
  assign PC_CK = and_102_out ? and_102_out : 1'bz;  // Driver driver_413
  assign driver_414_out = and_102_out ? and_102_out : 1'bz;  // Driver driver_414
  assign driver_415_out = and_102_out ? and_102_out : 1'bz;  // Driver driver_415
  assign driver_416_out = and_102_out ? and_102_out : 1'bz;  // Driver driver_416
  Driver driver_417 (.in(and_102_out), .en(and_102_out));  // open: out
  and and_107 (CNT_JMP, JMP, NOIND, CK1);
  and and_108 (and_108_out, JMP, NOIND, STB1);
  LED led_201 (.in(CNT_JMP));
  LED led_202 (.in(and_108_out));
  assign IR2PC = CNT_JMP ? CNT_JMP : 1'bz;  // Driver driver_418
  assign PC_LD = CNT_JMP ? CNT_JMP : 1'bz;  // Driver driver_419
  assign PC_CK = and_108_out ? and_108_out : 1'bz;  // Driver driver_420
  and and_109 (CNT_JMP_I, JMP, IND, CK1);
  and and_110 (and_110_out, JMP, IND, STB1);
  LED led_203 (.in(CNT_JMP_I));
  LED led_204 (.in(and_110_out));
  assign IR2RAMA = CNT_JMP_I ? CNT_JMP_I : 1'bz;  // Driver driver_421
  assign RAMD2PC = CNT_JMP_I ? CNT_JMP_I : 1'bz;  // Driver driver_422
  assign RAM_OE = CNT_JMP_I ? CNT_JMP_I : 1'bz;  // Driver driver_423
  assign PC_LD = CNT_JMP_I ? CNT_JMP_I : 1'bz;  // Driver driver_424
  assign driver_425_out = CNT_JMP_I ? CNT_JMP_I : 1'bz;  // Driver driver_425
  Driver driver_426 (.in(and_110_out), .en(and_110_out));  // open: out
  Driver driver_427 (.in(and_110_out), .en(and_110_out));  // open: out
  Driver driver_428 (.in(and_110_out), .en(and_110_out));  // open: out
  assign PC_LD = and_110_out ? and_110_out : 1'bz;  // Driver driver_429
  assign PC_CK = and_110_out ? and_110_out : 1'bz;  // Driver driver_430
  and and_111 (and_111_out, JMP, AUTOIND, CK3);
  and and_112 (and_112_out, JMP, AUTOIND, STB3);
  and and_113 (CNT_JMP_IA, JMP, AUTOIND, CK1);
  and and_114 (and_114_out, JMP, AUTOIND, STB1);
  and and_115 (and_115_out, JMP, AUTOIND, CK2);
  and and_116 (and_116_out, JMP, AUTOIND, STB2);
  LED led_205 (.in(and_111_out));
  LED led_206 (.in(and_112_out));
  LED led_207 (.in(CNT_JMP_IA));
  LED led_208 (.in(and_114_out));
  LED led_209 (.in(and_115_out));
  LED led_210 (.in(and_116_out));
  assign IR2RAMA = and_111_out ? and_111_out : 1'bz;  // Driver driver_431
  assign RAMD2PC = and_111_out ? and_111_out : 1'bz;  // Driver driver_432
  assign RAM_OE = and_111_out ? and_111_out : 1'bz;  // Driver driver_433
  assign PC_LD = and_111_out ? and_111_out : 1'bz;  // Driver driver_434
  assign driver_435_out = and_111_out ? and_111_out : 1'bz;  // Driver driver_435
  Driver driver_436 (.in(and_112_out), .en(and_112_out));  // open: out
  Driver driver_437 (.in(and_112_out), .en(and_112_out));  // open: out
  Driver driver_438 (.in(and_112_out), .en(and_112_out));  // open: out
  Driver driver_439 (.in(and_112_out), .en(and_112_out));  // open: out
  assign PC_CK = and_112_out ? and_112_out : 1'bz;  // Driver driver_440
  assign IR2RAMA = CNT_JMP_IA ? CNT_JMP_IA : 1'bz;  // Driver driver_441
  assign RAM_OE = CNT_JMP_IA ? CNT_JMP_IA : 1'bz;  // Driver driver_442
  assign IND2INC = CNT_JMP_IA ? CNT_JMP_IA : 1'bz;  // Driver driver_443
  assign IND_CK = and_114_out ? and_114_out : 1'bz;  // Driver driver_444
  assign INC2RAMD = and_115_out ? and_115_out : 1'bz;  // Driver driver_445
  assign IND2INC = and_115_out ? and_115_out : 1'bz;  // Driver driver_446
  assign IR2RAMA = and_115_out ? and_115_out : 1'bz;  // Driver driver_447
  assign RAM_WE = and_116_out ? and_116_out : 1'bz;  // Driver driver_448
  and and_117 (CNT_OPR1, OPR1, 1'b1, CK1);
  and and_118 (and_118_out, OPR1, 1'b1, STB1);
  LED led_211 (.in(CNT_OPR1));
  LED led_212 (.in(and_118_out));
  assign ROT2AC = CNT_OPR1 ? CNT_OPR1 : 1'bz;  // Driver driver_449
  assign LINK_CK = and_118_out ? and_118_out : 1'bz;  // Driver driver_450
  assign AC_CK = and_118_out ? and_118_out : 1'bz;  // Driver driver_451
  and and_119 (CNT_OPR2, OPR2, 1'b1, CK1);
  and and_120 (and_120_out, OPR2, SKIP, STB1);
  and and_121 (and_121_out, OPR2, 1'b1, CK2);
  LED led_213 (.in(and_121_out));
  and and_122 (and_122_out, OPR2, 1'b1, STB2);
  assign ROT2AC = CNT_OPR2 ? CNT_OPR2 : 1'bz;  // Driver driver_452
  LED led_214 (.in(CNT_OPR2));
  Driver driver_453 (.in(CNT_OPR2), .en(CNT_OPR2));  // open: out
  Driver driver_454 (.in(CNT_OPR2), .en(CNT_OPR2));  // open: out
  Driver driver_455 (.in(CNT_OPR2), .en(CNT_OPR2));  // open: out
  Driver driver_456 (.in(CNT_OPR2), .en(CNT_OPR2));  // open: out
  assign driver_457_out = and_120_out ? and_120_out : 1'bz;  // Driver driver_457
  LED led_215 (.in(and_120_out));
  assign PC_CK = and_120_out ? and_120_out : 1'bz;  // Driver driver_458
  Driver driver_459 (.in(and_120_out), .en(and_120_out));  // open: out
  Driver driver_460 (.in(and_120_out), .en(and_120_out));  // open: out
  Driver driver_461 (.in(and_120_out), .en(and_120_out));  // open: out
  assign ROT2AC = and_121_out ? and_121_out : 1'bz;  // Driver driver_462
  Driver driver_463 (.in(and_121_out), .en(and_121_out));  // open: out
  Driver driver_464 (.in(and_121_out), .en(and_121_out));  // open: out
  Driver driver_465 (.in(and_121_out), .en(and_121_out));  // open: out
  Driver driver_466 (.in(and_121_out), .en(and_121_out));  // open: out
  Driver driver_467 (.in(and_122_out), .en(and_122_out));  // open: out
  LED led_216 (.in(and_122_out));
  assign AC_CK = and_122_out ? and_122_out : 1'bz;  // Driver driver_468
  Driver driver_469 (.in(and_122_out), .en(and_122_out));  // open: out
  Driver driver_470 (.in(and_122_out), .en(and_122_out));  // open: out
  Driver driver_471 (.in(and_122_out), .en(and_122_out));  // open: out
  not not_4 (not_4_out, OPR_SWP);
  not not_5 (not_5_out, OPR_SWP);
  and and_123 (CNT_OPR3, OPR3, 1'b1, CK1);
  and and_124 (and_124_out, OPR3, not_4_out, STB1);
  and and_125 (and_125_out, OPR3, 1'b1, CK2);
  and and_126 (and_126_out, OPR3, not_5_out, STB2);
  LED led_217 (.in(CNT_OPR3));
  LED led_218 (.in(and_124_out));
  LED led_219 (.in(and_125_out));
  LED led_220 (.in(and_126_out));
  assign ROT2AC = CNT_OPR3 ? CNT_OPR3 : 1'bz;  // Driver driver_472
  Driver driver_473 (.in(CNT_OPR3), .en(CNT_OPR3));  // open: out
  Driver driver_474 (.in(CNT_OPR3), .en(CNT_OPR3));  // open: out
  Driver driver_475 (.in(CNT_OPR3), .en(CNT_OPR3));  // open: out
  Driver driver_476 (.in(CNT_OPR3), .en(CNT_OPR3));  // open: out
  Driver driver_477 (.in(and_124_out), .en(and_124_out));  // open: out
  Driver driver_478 (.in(and_124_out), .en(and_124_out));  // open: out
  assign MQ_CK = and_124_out ? and_124_out : 1'bz;  // Driver driver_479
  Driver driver_480 (.in(and_124_out), .en(and_124_out));  // open: out
  Driver driver_481 (.in(and_124_out), .en(and_124_out));  // open: out
  Driver driver_482 (.in(and_124_out), .en(and_124_out));  // open: out
  assign ROT2AC = and_125_out ? and_125_out : 1'bz;  // Driver driver_483
  Driver driver_484 (.in(and_125_out), .en(and_125_out));  // open: out
  Driver driver_485 (.in(and_125_out), .en(and_125_out));  // open: out
  Driver driver_486 (.in(and_125_out), .en(and_125_out));  // open: out
  Driver driver_487 (.in(and_125_out), .en(and_125_out));  // open: out
  Driver driver_488 (.in(and_126_out), .en(and_126_out));  // open: out
  assign AC_CK = and_126_out ? and_126_out : 1'bz;  // Driver driver_489
  Driver driver_490 (.in(and_126_out), .en(and_126_out));  // open: out
  Driver driver_491 (.in(and_126_out), .en(and_126_out));  // open: out
  Driver driver_492 (.in(and_126_out), .en(and_126_out));  // open: out
  and and_127 (and_127_out, OPR3, OPR_SWP, STB1);
  assign MQ_CK = and_127_out ? and_127_out : 1'bz;  // Driver driver_493
  LED led_221 (.in(and_127_out));
  assign AC_CK = and_127_out ? and_127_out : 1'bz;  // Driver driver_494
  Driver driver_495 (.in(and_127_out), .en(and_127_out));  // open: out
  Driver driver_496 (.in(and_127_out), .en(and_127_out));  // open: out
  Driver driver_497 (.in(and_127_out), .en(and_127_out));  // open: out
  or or_10 (or_10_out, CK1, CK2, CK3, CK4, CK5, CK6, CK7, CK8, CK9);
  LED led_222 (.in(IOT));
  Demultiplexer #(.Selector_Bits(3)) demultiplexer_1 (
    .sel(BUS_IR[2:0]), .in(IOT_DEVKBD), .out_0(INST_KCF), .out_1(INST_KSF), .out_2(INST_KCC),
    .out_3(demultiplexer_1_out_3), .out_4(INST_KRS), .out_5(INST_KIE), .out_6(INST_KRB),
    .out_7(demultiplexer_1_out_7));
  LED led_223 (.in(IOT_DEVKBD));
  Demultiplexer #(.Selector_Bits(3)) demultiplexer_2 (
    .sel(BUS_IR[2:0]), .in(IOT_DEVPRI), .out_0(INST_TFL), .out_1(INST_TSF), .out_2(INST_TCF),
    .out_3(demultiplexer_2_out_3), .out_4(INST_TPC), .out_5(INST_TSK), .out_6(INST_TLS),
    .out_7(demultiplexer_2_out_7));
  LED led_224 (.in(IOT_DEVPRI));
  Demultiplexer #(.Selector_Bits(3)) demultiplexer_3 (
    .sel(BUS_IR[2:0]), .in(IOT_DEVHSR), .out_0(demultiplexer_3_out_0), .out_1(demultiplexer_3_out_1),
    .out_2(demultiplexer_3_out_2), .out_3(demultiplexer_3_out_3), .out_4(demultiplexer_3_out_4),
    .out_5(demultiplexer_3_out_5), .out_6(demultiplexer_3_out_6), .out_7(demultiplexer_3_out_7));
  LED led_225 (.in(IOT_DEVHSR));
  Demultiplexer #(.Selector_Bits(3)) demultiplexer_4 (
    .sel(BUS_IR[2:0]), .in(IOT_DEVCPU), .out_0(IOT_SKON), .out_1(IOT_ION), .out_2(IOT_IOF), .out_3(IOT_SRQ),
    .out_4(IOT_GTF), .out_5(IOT_RTF), .out_6(IOT_SGT), .out_7(IOT_CAF));
  LED led_226 (.in(IOT_DEVCPU));
  // Probe on BUS_IR[2:0]
  // Probe on BUS_IR[8:3]
  and and_128 (and_128_out, or_10_out, IOT);
  Demultiplexer #(.Selector_Bits(6)) demultiplexer_5 (
    .sel(BUS_IR[8:3]), .in(and_128_out), .out_0(IOT_DEVCPU), .out_1(IOT_DEVHSR), .out_2(IOT_DEVHSP),
    .out_3(IOT_DEVKBD), .out_4(IOT_DEVPRI), .out_5(IOT_5), .out_6(IOT_6), .out_7(IOT_7), .out_8(IOT_8),
    .out_9(IOT_9), .out_10(demultiplexer_5_out_10), .out_11(demultiplexer_5_out_11),
    .out_12(demultiplexer_5_out_12), .out_13(demultiplexer_5_out_13), .out_14(demultiplexer_5_out_14),
    .out_15(demultiplexer_5_out_15), .out_16(demultiplexer_5_out_16), .out_17(demultiplexer_5_out_17),
    .out_18(demultiplexer_5_out_18), .out_19(demultiplexer_5_out_19), .out_20(demultiplexer_5_out_20),
    .out_21(demultiplexer_5_out_21), .out_22(demultiplexer_5_out_22), .out_23(demultiplexer_5_out_23),
    .out_24(demultiplexer_5_out_24), .out_25(demultiplexer_5_out_25), .out_26(demultiplexer_5_out_26),
    .out_27(demultiplexer_5_out_27), .out_28(demultiplexer_5_out_28), .out_29(demultiplexer_5_out_29),
    .out_30(demultiplexer_5_out_30), .out_31(demultiplexer_5_out_31), .out_32(demultiplexer_5_out_32),
    .out_33(demultiplexer_5_out_33), .out_34(demultiplexer_5_out_34), .out_35(demultiplexer_5_out_35),
    .out_36(demultiplexer_5_out_36), .out_37(demultiplexer_5_out_37), .out_38(demultiplexer_5_out_38),
    .out_39(demultiplexer_5_out_39), .out_40(demultiplexer_5_out_40), .out_41(demultiplexer_5_out_41),
    .out_42(demultiplexer_5_out_42), .out_43(demultiplexer_5_out_43), .out_44(demultiplexer_5_out_44),
    .out_45(demultiplexer_5_out_45), .out_46(demultiplexer_5_out_46), .out_47(demultiplexer_5_out_47),
    .out_48(demultiplexer_5_out_48), .out_49(demultiplexer_5_out_49), .out_50(demultiplexer_5_out_50),
    .out_51(demultiplexer_5_out_51), .out_52(demultiplexer_5_out_52), .out_53(demultiplexer_5_out_53),
    .out_54(demultiplexer_5_out_54), .out_55(demultiplexer_5_out_55), .out_56(demultiplexer_5_out_56),
    .out_57(demultiplexer_5_out_57), .out_58(demultiplexer_5_out_58), .out_59(demultiplexer_5_out_59),
    .out_60(demultiplexer_5_out_60), .out_61(demultiplexer_5_out_61), .out_62(demultiplexer_5_out_62),
    .out_63(demultiplexer_5_out_63));
  Seven_Seg_Hex seven_seg_hex_40 (.d(CK_NUM), .dp(1'b0));
  or or_11 (IOT_5x, demultiplexer_5_out_50, demultiplexer_5_out_51, demultiplexer_5_out_52, demultiplexer_5_out_53, demultiplexer_5_out_54, demultiplexer_5_out_56, demultiplexer_5_out_57, demultiplexer_5_out_58, demultiplexer_5_out_59, demultiplexer_5_out_55);
  or or_12 (IOT_6x, demultiplexer_5_out_60, demultiplexer_5_out_61, demultiplexer_5_out_63, demultiplexer_5_out_62);
  // Probe on LATCHED_PC
  or or_13 (IOT_3x, demultiplexer_5_out_30, demultiplexer_5_out_31, demultiplexer_5_out_32, demultiplexer_5_out_33, demultiplexer_5_out_34, demultiplexer_5_out_36, demultiplexer_5_out_37, demultiplexer_5_out_38, demultiplexer_5_out_39, demultiplexer_5_out_35);
  or or_14 (IOT_4x, demultiplexer_5_out_40, demultiplexer_5_out_41, demultiplexer_5_out_42, demultiplexer_5_out_43, demultiplexer_5_out_44, demultiplexer_5_out_46, demultiplexer_5_out_47, demultiplexer_5_out_48, demultiplexer_5_out_49, demultiplexer_5_out_45);
  LED led_227 (.in(PH_FIRST));
  LED led_228 (.in(PH_STB));
  or or_15 (IOT_1x, demultiplexer_5_out_10, demultiplexer_5_out_11, demultiplexer_5_out_12, demultiplexer_5_out_13, demultiplexer_5_out_14, demultiplexer_5_out_16, demultiplexer_5_out_17, demultiplexer_5_out_18, demultiplexer_5_out_19, demultiplexer_5_out_15);
  or or_16 (IOT_2x, demultiplexer_5_out_20, demultiplexer_5_out_21, demultiplexer_5_out_22, demultiplexer_5_out_23, demultiplexer_5_out_24, demultiplexer_5_out_26, demultiplexer_5_out_27, demultiplexer_5_out_28, demultiplexer_5_out_29, demultiplexer_5_out_25);
  LED led_229 (.in(PH_LAST));
  // Probe on BUS_IR
  Demultiplexer #(.Selector_Bits(3)) demultiplexer_6 (
    .sel(BUS_IR[11:9]), .in(1'b1), .out_0(AND), .out_1(TAD), .out_2(ISZ), .out_3(DCA), .out_4(JMS),
    .out_5(JMP), .out_6(IOT), .out_7(OPR));
  LED led_230 (.in(OPR));
  Demultiplexer #(.Selector_Bits(2)) demultiplexer_7 (
    .sel({BUS_IR[8], BUS_IR[0]}), .in(OPR), .out_0(demultiplexer_7_out_0), .out_1(demultiplexer_7_out_1),
    .out_2(OPR2), .out_3(OPR3));
  and and_129 (and_129_out, BUS_IR[3], ~BUS_IR[4], ~BUS_IR[5], ~BUS_IR[6], ~BUS_IR[7], BUS_IR[8]);  // And
  LED led_231 (.in(and_129_out));
  not not_6 (not_6_out, BUS_IR[8]);
  or or_17 (OPR1, demultiplexer_7_out_0, demultiplexer_7_out_1);
  nor nor_2 (nor_2_out, and_129_out, not_6_out);
  LED led_232 (.in(OPR1));
  LED led_233 (.in(nor_2_out));
  nor nor_3 (nor_3_out, OPR, IOT);
  nor nor_4 (nor_4_out, BUS_IR[0], BUS_IR[1], BUS_IR[2], BUS_IR[3], BUS_IR[4], BUS_IR[5], BUS_IR[6], BUS_IR[7]);
  and and_130 (AUTOIND, nor_3_out, and_129_out);
  and and_131 (IND, nor_3_out, nor_2_out);
  and and_132 (NOIND, nor_3_out, not_6_out);
  and and_133 (MP, nor_3_out, BUS_IR[7]);
  and and_134 (OPR_IAC, BUS_IR[0], OPR1);
  LED led_234 (.in(OPR_IAC));
  and and_135 (OPR_X2, BUS_IR[1], OPR1);
  LED led_235 (.in(OPR_X2));
  and and_136 (OPR_LEFT, BUS_IR[2], OPR1);
  LED led_236 (.in(OPR_LEFT));
  and and_137 (OPR_RIGHT, BUS_IR[3], OPR1);
  LED led_237 (.in(OPR_RIGHT));
  and and_138 (OPR_CML, BUS_IR[4], OPR1);
  LED led_238 (.in(OPR_CML));
  and and_139 (OPR_CMA, BUS_IR[5], OPR1);
  LED led_239 (.in(OPR_CMA));
  and and_140 (OPR_CLL, BUS_IR[6], OPR1);
  LED led_240 (.in(OPR_CLL));
  and and_141 (OPR_CLA1, BUS_IR[7], OPR1);
  LED led_241 (.in(OPR_CLA1));
  and and_142 (OPR_NA1, BUS_IR[0], OPR2);
  LED led_242 (.in(OPR_NA1));
  and and_143 (OPR_HLT, BUS_IR[1], OPR2);
  LED led_243 (.in(OPR_HLT));
  and and_144 (OPR_OSR, BUS_IR[2], OPR2);
  LED led_244 (.in(OPR_OSR));
  and and_145 (OPR_TSTINV, BUS_IR[3], OPR2);
  LED led_245 (.in(OPR_TSTINV));
  and and_146 (OPR_SNLSZL, BUS_IR[4], OPR2);
  LED led_246 (.in(OPR_SNLSZL));
  and and_147 (OPR_SZASNA, BUS_IR[5], OPR2);
  LED led_247 (.in(OPR_SZASNA));
  and and_148 (OPR_SMASPA, BUS_IR[6], OPR2);
  LED led_248 (.in(OPR_SMASPA));
  and and_149 (OPR_CLA2, BUS_IR[7], OPR2);
  LED led_249 (.in(OPR_CLA2));
  and and_150 (and_150_out, OPR3, BUS_IR[0]);
  and and_151 (and_151_out[0], OPR3, BUS_IR[1]);
  and and_152 (and_151_out[1], OPR3, BUS_IR[2]);
  and and_153 (and_151_out[2], OPR3, BUS_IR[3]);
  and and_154 (and_154_out, OPR3, BUS_IR[4]);
  and and_155 (OPR_SCA, OPR3, BUS_IR[5]);
  and and_156 (and_156_out, OPR3, BUS_IR[6]);
  and and_157 (OPR_CLA3, OPR3, BUS_IR[7]);
  LED led_250 (.in(AUTOIND));
  LED led_251 (.in(IND));
  LED led_252 (.in(NOIND));
  LED led_253 (.in(MP));
  LED led_254 (.in(OPR3));
  LED led_255 (.in(and_150_out));
  LED led_256 (.in(and_151_out[0]));
  LED led_257 (.in(and_151_out[1]));
  LED led_258 (.in(and_151_out[2]));
  LED led_259 (.in(and_154_out));
  LED led_260 (.in(OPR_SCA));
  LED led_261 (.in(and_156_out));
  LED led_262 (.in(OPR_CLA3));
  and and_158 (OPR_NOP, nor_4_out, OPR);
  LED led_263 (.in(OPR1));
  LED led_264 (.in(OPR2));
  nand nand_1 (nand_1_out, and_154_out, and_156_out);
  LED led_265 (.in(OPR_NOP));
  LED led_266 (.in(nand_1_out));
  Seven_Seg_Hex seven_seg_hex_41 (.d(CK_NUM), .dp(1'b0));
  and and_159 (OPR_MQL, and_154_out, and_154_out);
  not not_7 (OPR_SWP, nand_1_out);
  and and_160 (OPR_MQA, and_156_out, and_156_out);
  // Probe on LATCHED_PC
  LED led_267 (.in(PH_FIRST));
  LED led_268 (.in(OPR_MQL));
  LED led_269 (.in(OPR_MQA));
  LED led_270 (.in(PH_STB));
  LED led_271 (.in(PH_LAST));
  Decoder #(.Selector_Bits(3)) decoder_1 (
    .sel(and_151_out), .out_0(OPR_OPERATION), .out_1(OPR_SCL), .out_2(OPR_MUY), .out_3(OPR_DVI),
    .out_4(OPR_NMI), .out_5(OPR_SHL), .out_6(OPR_ASL), .out_7(OPR_LSR));
  LED led_272 (.in(OPR_OPERATION));
  LED led_273 (.in(OPR_SCL));
  LED led_274 (.in(OPR_MUY));
  LED led_275 (.in(OPR_DVI));
  LED led_276 (.in(OPR_NMI));
  LED led_277 (.in(OPR_SHL));
  LED led_278 (.in(OPR_ASL));
  LED led_279 (.in(OPR_LSR));
  PullDown pulldown_4 (.out(IR2PC));
  PullDown pulldown_5 (.out(IND2PC));
  PullDown pulldown_6 (.out(RAMD2PC));
  PullDown pulldown_7 (.out(ROT2AC));
  PullDown pulldown_8 (.out(RAMD2AC_ADD));
  PullDown pulldown_9 (.out(PC_LD));
  PullDown pulldown_10 (.out(IND2RAMA));
  PullDown pulldown_11 (.out(INC2RAMD));
  PullDown pulldown_12 (.out(PC2RAMD));
  PullDown pulldown_13 (.out(IR2RAMA));
  PullDown pulldown_14 (.out(IND2INC));
  PullDown pulldown_15 (.out(LD2INC));
  PullDown pulldown_16 (.out(RAMA_HOLD));
  PullDown pulldown_17 (.out(DATA_CK));
  PullDown pulldown_18 (.out(IR_CK));
  PullDown pulldown_19 (.out(PC_CK));
  PullDown pulldown_20 (.out(AC_CK));
  PullDown pulldown_21 (.out(IND_CK));
  PullDown pulldown_22 (.out(LINK_CK));
  PullDown pulldown_23 (.out(RAM_WE));
  PullDown pulldown_24 (.out(RAM_OE));
  PullDown pulldown_25 (.out(MQ_CK));
  and and_161 (i_iac, OPR_IAC, 1'b1);
  and and_162 (i_cll, OPR_CLL, 1'b1);
  and and_163 (i_cma, OPR_CMA, 1'b1);
  and and_164 (i_cml, OPR_CML, 1'b1);
  and and_165 (i_osr, OPR_OSR, 1'b1);
  and and_166 (i_hlt, OPR_HLT, 1'b1);
  or or_18 (i_cla, OPR_CLA1, OPR_CLA2);
  and and_167 (i_nop, OPR_NOP, 1'b1);
  and and_168 (i_ral, OPR_LEFT, ~OPR_X2);  // And
  and and_169 (i_rar, OPR_RIGHT, ~OPR_X2);  // And
  and and_170 (i_rtl, OPR_LEFT, OPR_X2);
  and and_171 (i_rtr, OPR_RIGHT, OPR_X2);
  and and_172 (i_snl, OPR_SNLSZL, ~OPR_TSTINV);  // And
  and and_173 (i_sza, OPR_SZASNA, ~OPR_TSTINV);  // And
  and and_174 (i_sma, OPR_SMASPA, ~OPR_TSTINV);  // And
  and and_175 (i_szl, OPR_SNLSZL, OPR_TSTINV);
  and and_176 (i_sna, OPR_SZASNA, OPR_TSTINV);
  and and_177 (i_spa, OPR_SMASPA, OPR_TSTINV);
  and and_178 (i_skp, ~OPR_SNLSZL, ~OPR_SZASNA, ~OPR_SMASPA, OPR_TSTINV);  // And

  // Other names for the same wires on the sheet: RAMADDR[11:0] = {RA3, RA2, RA1, RA0}; PI0[2:0] = PCIN[2:0];
  //   PI1[2:0] = PCIN[5:3]; PI2[2:0] = PCIN[8:6]; PI3[2:0] = PCIN[11:9]; AC0[2:0] = AC[2:0]; AC1[2:0] = AC[5:3];
  //   AC2[2:0] = AC[8:6]; AC3[2:0] = AC[11:9]; IR0[2:0] = BUS_IR[2:0]; IR1[2:0] = BUS_IR[5:3]; IR2[2:0] = BUS_IR[8:6];
  //   IR3[2:0] = BUS_IR[11:9]; PC0[2:0] = BUS_PC[2:0]; PC1[2:0] = BUS_PC[5:3]; PC2[2:0] = BUS_PC[8:6];
  //   PC3[2:0] = BUS_PC[11:9]; DATA[11:0] = {DA3, DA2, DA1, DA0}; INDOUT[11:0] = {IND3, IND2, IND1, IND0};
  //   MQ0[2:0] = MQ[2:0]; MQ1[2:0] = MQ[5:3]; MQ2[2:0] = MQ[8:6]; MQ3[2:0] = MQ[11:9]; RD0[2:0] = RAMDATA[2:0];
  //   RD1[2:0] = RAMDATA[5:3]; RD2[2:0] = RAMDATA[8:6]; RD3[2:0] = RAMDATA[11:9]; XTAL = clk

  // Notes on the sheet:
  //   clk: Hz: 10000
  //   PCIN
  //   PC
  //   IR
  //   AC
  //   MQ
  //   IND
  //   RAM-A
  //   RAM-D
  //   PC-IN
  //   DATA
  //   ACCUMULATOR
  //   PCOUT
  //   C
  //   LINK
  //   KCF
  //   NOP
  //   AND
  //   TAD
  //   KSF
  //   CLA
  //   STATE
  //   INSTRUCTION
  //   RUN
  //   HALT
  //   PC=0200
  //   BREAKPOINT
  //   MAIN DATA-PATHS
  //   RAMADDR
  //   KCC
  //   KRS
  //   CLL
  //   ISZ
  //   DCA
  //   KIE
  //   CMA
  //   JMS
  //   START/STOP/STEP
  //   CLOCK CYCLE CONTROLLER
  //   contents of eeprom_1 (hex, n*v repeats v):
  //   0,a01,2,3,0,0,f02,e00,0,f02,f02,f02,f02,f02,f02,f02,0,1,2,3,4,6,8,c,10,18,20,30,40,
  //   60,80,c0,100,180,200,29c,300,400,600,6ca,800,fcf,ffe,ffd,ffb,ff7,fef,fdf,e7f,fbf,
  //   f7f,eff,dff,bff,7ff,fff,aaa,555,c00,e00,f00,f80,fe0,ff0,ff8,ffc,7,37,f,1f,3f,7f,ff,
  //   1ff,3ff,fc0,a95,56a,1f8,e07,87,a60,a60,f02,f02,f02,f02,f02,f02,f02,f02,f02,f02,f02,
  //   f02,f02,f02,f02,f02,f02,237,e80,f02,f08,f02,e80,f20,f02,f28,f08,f02,e80,228,f20,f08,
  //   f02,f28,f02,e80,225,f20,f08,f02,f28,f02,e00,e00,f08,a64,e80,222,f20,f08,f02,f28,f02,
  //   e80,220,f20,f08,f02,f28,f02,e80,21e,f20,f08,f02,f28,f02,e80,21c,f20,f08,f02,f28,f02,
  //   e80,21a,f20,f08,f02,f28,f02,e80,218,f20,f08,f02,f28,f02,e80,216,f20,f08,f02,f28,f02,
  //   e80,214,f20,f08,f02,f28,f02,e80,212,f20,f08,f02,f28,f02,e80,211,f20,f08,f02,f28,f02,
  //   e80,236,f48,f02,e80,228,f48,f08,f02,e80,236,f40,f08,f02,e80,228,f40,f02,e80,237,e20,
  //   f20,f02,e80,239,e20,f28,f02,239,e20,f20,f02,e80,238,e20,f28,f02,238,e20,f20,f02,e80,
  //   237,e20,f20,f02,e80,e01,f20,f08,f02,e80,237,e01,f20,f02,e80,241,e01,e01,e01,e01,f20,
  //   f02,e80,e40,e04,f18,f02,e80,e40,e10,228,e04,f18,f08,f02,e80,e40,e04,f10,f08,f02,e80,
  //   e40,e10,228,e04,f10,f02,e80,228,e04,f10,aaa,e40,f18,f02,aae,e10,f10,f02,aa6,e40,f18,
  //   f02,e10,f10,f02,e10,f18,f02,e80,237,f80,f20,f02,e80,f04,e20,f20,f02,e80,e40,e00,f28,
  //   f18,f02,e80,e40,f00,f28,f18,f02,e80,236,228,e20,f20,f02,e80,235,225,e20,f20,f02,e80,
  //   234,222,e20,f20,f02,e80,233,220,e20,f20,f02,e80,232,21e,e20,f20,f02,e80,231,21c,e20,
  //   f20,f02,e80,22f,21a,e20,f20,f02,e80,22e,218,e20,f20,f02,e80,22d,216,e20,f20,f02,e80,
  //   22c,214,e20,f20,f02,e80,22b,212,e20,f20,f02,e80,22a,211,e20,f20,f02,e80,e40,228,228,
  //   f18,f20,f02,e80,e40,23a,225,f18,f20,f02,e80,e40,23b,222,f18,f20,f02,e80,e40,23c,220,
  //   f18,f20,f02,e80,e40,23d,21e,f18,f20,f02,e80,e40,24b,21c,f18,f20,f02,e80,e40,23e,21a,
  //   f18,f20,f02,e80,e40,23f,218,f18,f20,f02,e80,e40,240,216,f18,f20,f02,e80,e40,241,214,
  //   f18,f20,f02,e80,e40,22a,212,f18,f20,f02,e80,e40,237,211,f18,f20,f02,e80,e40,e10,228,
  //   228,f10,f20,f02,e80,e40,236,225,225,e20,f10,f20,f02,e80,e40,235,222,222,e20,f10,f20,
  //   f02,e80,e40,234,220,220,e20,f10,f20,f02,e80,e40,233,21e,21e,e20,f10,f20,f02,e80,e40,
  //   232,21c,21c,e20,f10,f20,f02,e80,e40,231,21a,21a,e20,f10,f20,f02,e80,e40,22f,218,218,
  //   e20,f10,f20,f02,e80,e40,22e,216,216,e20,f10,f20,f02,e80,e40,22d,214,214,e20,f10,f20,
  //   f02,e80,e40,22c,212,212,e20,f10,f20,f02,e80,e40,22b,211,211,e20,f10,f18,f02,e80,e40,
  //   211,213,22c,e20,f10,f20,f02,e80,e40,212,215,22d,e20,f10,f20,f02,e80,e40,214,217,22e,
  //   e20,f10,f20,f02,e80,e40,216,219,22f,e20,f10,f20,f02,e80,e40,218,21b,231,e20,f10,f20,
  //   f02,e80,e40,21a,21d,232,e20,f10,f20,f02,e80,e40,21c,21f,233,e20,f10,f20,f02,e80,e40,
  //   21e,221,234,e20,f10,f20,f02,e80,e40,220,224,235,e20,f10,f20,f02,e80,e40,222,226,236,
  //   e20,f10,f20,f02,e80,e40,225,23a,f18,f20,f02,e80,e40,237,211,f18,f20,f02,e80,e40,213,
  //   213,240,211,e20,f10,f20,f02,e80,e40,215,215,23f,213,e20,f10,f20,f02,e80,e40,217,217,
  //   23e,242,e20,f10,f20,f02,e80,e40,219,219,229,e20,f10,f20,f02,e80,e40,21b,21b,23d,245,
  //   e20,f10,f20,f02,e80,e40,21d,21d,23c,246,e20,f10,f20,f02,e80,e40,21f,21f,230,e20,f10,
  //   f20,f02,e80,e40,221,221,23a,248,e20,f10,f20,f02,e80,e40,224,224,228,249,e20,f10,f20,
  //   f02,e80,e40,226,226,24a,e20,f10,f20,f02,e80,e40,23a,23a,236,e20,f18,f20,f02,e80,e40,
  //   237,237,211,e20,f18,f20,f02,e80,e40,211,e08,f10,f02,e80,e40,210,e08,f20,f02,e80,e40,
  //   210,e08,f18,f02,e80,e40,e10,210,e08,f18,f02,e80,e40,e10,237,e08,e20,f20,f02,e80,e40,
  //   e10,210,e08,236,e20,f28,f18,f02,e80,e40,228,e08,235,e20,f28,f18,f02,e80,e40,225,e08,
  //   234,e20,f28,f18,f02,e80,e40,222,e08,233,e20,f28,f18,f02,e80,e40,220,e08,232,e20,f28,
  //   f18,f02,e80,e40,21e,e08,231,e20,f28,f18,f02,e80,e40,21c,e08,22f,e20,f28,f18,f02,e80,
  //   e40,21a,e08,22e,e20,f28,f18,f02,e80,e40,218,e08,22d,e20,f28,f18,f02,e80,e40,216,e08,
  //   22c,e20,f28,f18,f02,e80,e40,214,e08,22b,e20,f28,f18,f02,e80,e40,212,e08,22a,e20,f28,
  //   f18,f02,e80,e40,211,e08,237,e20,f28,f10,f02,e80,e40,212,e0a,f10,f02,e80,e40,210,e0a,
  //   f20,f02,e80,e40,210,e0a,f18,f02,e80,e40,e10,210,e0a,f18,f02,e80,e40,e10,237,e0a,e20,
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  //   KRB
  //   CML
  //   JMP
  //   RAMDATA
  //   TFL
  //   IAC
  //   IOT
  //   OPR
  //   TSF
  //   RAR
  //   RTR
  //   TCF
  //   RAL
  //   DIR
  //   SEQ OPR 1 MICROCODES
  //   ------------------------------------
  //   1 CLA CLL
  //   2 CMA CML
  //   3 IAC
  //   4 RAR RAL RTR RTL BSW
  //   TPC
  //   TSK
  //   RTL
  //   AUTO
  //   IND
  //   OSR
  //   TLS
  //   SKP
  //   CURR
  //   PAGE
  //   -
  //   0=Inst1 1=Inst2
  //   3=..... 4=.....
  //   5=..... 6=.....
  //   7=..... 8=.....
  //   ROTATES
  //   SZA
  //   SMA
  //   SPA
  //   SNA
  //   SWITCHES
  //   INDOUT
  //   SZL
  //   SNL
  //   BANK #
  //   HLT
  //   LATCHED
  //   DATA
  //   PDP-8/X
  //   Rev 0.2PA
  //   github.com/SmallRoomLabs/PDP8-X
  //   F
  //   S
  //   LATCHED PC
  //   L
  //   STEP
  //   PHASE
  //   AUTOINDEX
  //   INDIRECT
  //   FETCH OP &
  //   INCREMENT PC
  //   SKIP LOGIC
  //   AC=0
  //   AC negative
  //   LINK<>0
  //   IND
  //   STEP1
  //   IND
  //   STEP2
  //   AND i
  //   SEQ OPR 2 MICROCODES
  //   ------------------------------------
  //   1 SMA SPA SZA SZN SNK SZL SKP
  //   2 CLA
  //   3 OSR
  //   4 HLT
  //   SMA      7500  skip on minus AC
  //   SPA      7510  skip on plus AC
  //   SZA      7440  skip on zero AC
  //   SNA      7450  skip on non-zero AC
  //   SNL      7420  skip on non-zero link
  //   SZL      7430  skip on zero link
  //   AND-i-auto
  //   iAuto 1
  //   iAuto 2
  //   iAuto 3
  //   iAuto 4
  //   TAD
  //   STEP1
  //   TAD
  //   STEP2
  //   CONSOLE
  //   TTY/KBD
  //   TAD i
  //   TAD-i-auto
  //   Get address
  //   of M
  //   Save value
  //   from M
  //   indo LATDAT
  //   SKIP IF
  //   AC=ZERO
  //   ISZ i
  //   Save value
  //   from IND
  //   indo LATDAT
  //   ISZ-i-auto
  //   DCA i
  //   DCA-i-auto
  //   Actually increment
  //   PC
  //   Prepare to store
  //   return address
  //   Actually store
  //   return address
  //   Actually set
  //   PC
  //   Pause to accept
  //   new PC inc clk
  //   Prepate to store 
  //   return addr
  //   to [ind]
  //   Store return addr
  //   to [ind]
  //   JMS i
  //   JMS i-auto
  //   Prepare to set
  //   new PC
  //   Actually set
  //   new PC
  //   Prepare to set PC
  //   with new vector
  //   JMP i
  //   JMP i-auto
  //   OPR 1
  //   OPR 2
  //   OPR 3
  //   IOT DECODER
  //   IR DECODER
  //   OPR DECODER
endmodule
